// Logisim project TRABALHO_2_CIRC_DIGI_8_OPERACOES.circ as structural Verilog: 31 circuits, main circuit MAIN
module MAIN (
  input  PRESET,
  input  CLEAR,
  input  ON_OFF,
  input  LOAD
);

  wire A0, A1, A2, A3, B0, B1, B2, B3, CLK, display1_1_a, display1_1_b, display1_1_c, display1_1_d,
       display1_1_e, display1_1_f, display1_1_g, display1_2_a, display1_2_b, display1_2_c, display1_2_d,
       display1_2_e, display1_2_f, display1_2_g, display1_3_a, display1_3_b, display1_3_c, display1_3_d,
       display1_3_e, display1_3_f, display1_3_g, display1_4_a, display1_4_b, display1_4_c, display1_4_d,
       display1_4_e, display1_4_f, display1_4_g, display1_5_a, display1_5_b, display1_5_c, display1_5_d,
       display1_5_e, display1_5_f, display1_5_g, display1_6_a, display1_6_b, display1_6_c, display1_6_d,
       display1_6_e, display1_6_f, display1_6_g, display4_1_a, display4_1_b, display4_1_c, display4_1_d,
       display4_1_e, display4_1_f, display4_1_g, display5_decimal_1_a, display5_decimal_1_b,
       display5_decimal_1_c, display5_decimal_1_d, display5_decimal_1_e, display5_decimal_1_f,
       display5_decimal_1_g, display5_decimal_bit_mais_sign_1_a, display5_decimal_bit_mais_sign_1_b,
       display5_decimal_bit_mais_sign_1_c, display5_decimal_bit_mais_sign_1_d,
       display5_decimal_bit_mais_sign_1_e, display5_decimal_bit_mais_sign_1_f,
       display5_decimal_bit_mais_sign_1_g, display_hex_1_a, display_hex_1_b, display_hex_1_c,
       display_hex_1_d, display_hex_1_e, display_hex_1_f, display_hex_1_g, display_hex_2_a, display_hex_2_b,
       display_hex_2_c, display_hex_2_d, display_hex_2_e, display_hex_2_f, display_hex_2_g, display_hex_3_a,
       display_hex_3_b, display_hex_3_c, display_hex_3_d, display_hex_3_e, display_hex_3_f, display_hex_3_g,
       display_hex_4_a, display_hex_4_b, display_hex_4_c, display_hex_4_d, display_hex_4_e, display_hex_4_f,
       display_hex_4_g, display_hex_5_a, display_hex_5_b, display_hex_5_c, display_hex_5_d, display_hex_5_e,
       display_hex_5_f, display_hex_5_g, display_hex_6_a, display_hex_6_b, display_hex_6_c, display_hex_6_d,
       display_hex_6_e, display_hex_6_f, display_hex_6_g, display_hex_7_a, display_hex_7_b, display_hex_7_c,
       display_hex_7_d, display_hex_7_e, display_hex_7_f, display_hex_7_g, display_hex_8_a, display_hex_8_b,
       display_hex_8_c, display_hex_8_d, display_hex_8_e, display_hex_8_f, display_hex_8_g, display_hex_9_a,
       display_hex_9_b, display_hex_9_c, display_hex_9_d, display_hex_9_e, display_hex_9_f, display_hex_9_g,
       display_hex_10_a, display_hex_10_b, display_hex_10_c, display_hex_10_d, display_hex_10_e,
       display_hex_10_f, display_hex_10_g, display_hex_11_a, display_hex_11_b, display_hex_11_c,
       display_hex_11_d, display_hex_11_e, display_hex_11_f, display_hex_11_g, ula_1_doisbits, xor_1_out,
       xor_2_out;
  wire [2:0] contador_op_1_q0;
  wire [4:0] ula_1_s;

  Clock u_CLK (.out(CLK));
  _7_Segment_Display #(.decimalPoint("false")) u_7_segment_display_1 (
    .g(display_hex_1_g), .f(display_hex_1_f), .a(display_hex_1_a), .b(display_hex_1_b), .e(display_hex_1_e),
    .d(display_hex_1_d), .c(display_hex_1_c));
  _7_Segment_Display #(.decimalPoint("false")) u_7_segment_display_2 (
    .g(display_hex_2_g), .f(display_hex_2_f), .a(display_hex_2_a), .b(display_hex_2_b), .e(display_hex_2_e),
    .d(display_hex_2_d), .c(display_hex_2_c));
  DISPLAY_HEX display_hex_1 (
    .A1(1'b0), .A0(A3), .A3(1'b0), .A2(1'b0), .c(display_hex_1_c), .d(display_hex_1_d), .e(display_hex_1_e),
    .f(display_hex_1_f), .g(display_hex_1_g), .a(display_hex_1_a), .b(display_hex_1_b));
  _7_Segment_Display #(.decimalPoint("false")) u_7_segment_display_3 (
    .g(display_hex_3_g), .f(display_hex_3_f), .a(display_hex_3_a), .b(display_hex_3_b), .e(display_hex_3_e),
    .d(display_hex_3_d), .c(display_hex_3_c));
  DISPLAY_HEX display_hex_2 (
    .A1(1'b0), .A0(B3), .A3(1'b0), .A2(1'b0), .c(display_hex_2_c), .d(display_hex_2_d), .e(display_hex_2_e),
    .f(display_hex_2_f), .g(display_hex_2_g), .a(display_hex_2_a), .b(display_hex_2_b));
  _7_Segment_Display #(.decimalPoint("false")) u_7_segment_display_4 (
    .g(display_hex_4_g), .f(display_hex_4_f), .a(display_hex_4_a), .b(display_hex_4_b), .e(display_hex_4_e),
    .d(display_hex_4_d), .c(display_hex_4_c));
  DISPLAY_HEX display_hex_3 (
    .A1(1'b0), .A0(A2), .A3(1'b0), .A2(1'b0), .c(display_hex_3_c), .d(display_hex_3_d), .e(display_hex_3_e),
    .f(display_hex_3_f), .g(display_hex_3_g), .a(display_hex_3_a), .b(display_hex_3_b));
  DISPLAY_HEX display_hex_4 (
    .A1(1'b0), .A0(B2), .A3(1'b0), .A2(1'b0), .c(display_hex_4_c), .d(display_hex_4_d), .e(display_hex_4_e),
    .f(display_hex_4_f), .g(display_hex_4_g), .a(display_hex_4_a), .b(display_hex_4_b));
  DISPLAY_HEX display_hex_5 (
    .A1(1'b0), .A0(A1), .A3(1'b0), .A2(1'b0), .c(display_hex_5_c), .d(display_hex_5_d), .e(display_hex_5_e),
    .f(display_hex_5_f), .g(display_hex_5_g), .a(display_hex_5_a), .b(display_hex_5_b));
  _7_Segment_Display #(.decimalPoint("false")) u_7_segment_display_5 (
    .g(display_hex_5_g), .f(display_hex_5_f), .a(display_hex_5_a), .b(display_hex_5_b), .e(display_hex_5_e),
    .d(display_hex_5_d), .c(display_hex_5_c));
  DISPLAY_HEX display_hex_6 (
    .A1(1'b0), .A0(B1), .A3(1'b0), .A2(1'b0), .c(display_hex_6_c), .d(display_hex_6_d), .e(display_hex_6_e),
    .f(display_hex_6_f), .g(display_hex_6_g), .a(display_hex_6_a), .b(display_hex_6_b));
  _7_Segment_Display #(.decimalPoint("false")) u_7_segment_display_6 (
    .g(display_hex_6_g), .f(display_hex_6_f), .a(display_hex_6_a), .b(display_hex_6_b), .e(display_hex_6_e),
    .d(display_hex_6_d), .c(display_hex_6_c));
  CONTADOR_1 contador_1_1 (.PRESET(PRESET), .CLEAR(CLEAR), .CLK(CLK), .LOAD(LOAD), .Q0(A0), .Q1(A1), .Q2(A2), .Q3(A3));
  CONTADOR_2 contador_2_1 (.PRESET(PRESET), .CLEAR(CLEAR), .CLK(CLK), .LOAD(LOAD), .Q0(B0), .Q1(B1), .Q2(B2), .Q3(B3));
  CONTADOR_OP contador_op_1 (
    .PRESET(PRESET), .CLEAR(CLEAR), .CLK(CLK), .LOAD(LOAD), .Q0(contador_op_1_q0[0]),
    .Q1(contador_op_1_q0[1]), .Q2(contador_op_1_q0[2]));
  DISPLAY_HEX display_hex_7 (
    .A1(1'b0), .A0(A0), .A3(1'b0), .A2(1'b0), .c(display_hex_7_c), .d(display_hex_7_d), .e(display_hex_7_e),
    .f(display_hex_7_f), .g(display_hex_7_g), .a(display_hex_7_a), .b(display_hex_7_b));
  _7_Segment_Display #(.decimalPoint("false")) u_7_segment_display_7 (
    .g(display_hex_7_g), .f(display_hex_7_f), .a(display_hex_7_a), .b(display_hex_7_b), .e(display_hex_7_e),
    .d(display_hex_7_d), .c(display_hex_7_c));
  DISPLAY_HEX display_hex_8 (
    .A1(1'b0), .A0(B0), .A3(1'b0), .A2(1'b0), .c(display_hex_8_c), .d(display_hex_8_d), .e(display_hex_8_e),
    .f(display_hex_8_f), .g(display_hex_8_g), .a(display_hex_8_a), .b(display_hex_8_b));
  _7_Segment_Display #(.decimalPoint("false")) u_7_segment_display_8 (
    .g(display_hex_8_g), .f(display_hex_8_f), .a(display_hex_8_a), .b(display_hex_8_b), .e(display_hex_8_e),
    .d(display_hex_8_d), .c(display_hex_8_c));
  DISPLAY_HEX display_hex_9 (
    .A1(A1), .A0(A0), .A3(A3), .A2(A2), .c(display_hex_9_c), .d(display_hex_9_d), .e(display_hex_9_e),
    .f(display_hex_9_f), .g(display_hex_9_g), .a(display_hex_9_a), .b(display_hex_9_b));
  DISPLAY_HEX display_hex_10 (
    .A1(B1), .A0(B0), .A3(B3), .A2(B2), .c(display_hex_10_c), .d(display_hex_10_d), .e(display_hex_10_e),
    .f(display_hex_10_f), .g(display_hex_10_g), .a(display_hex_10_a), .b(display_hex_10_b));
  DISPLAY_HEX display_hex_11 (
    .A1(contador_op_1_q0[1]), .A0(contador_op_1_q0[0]), .A3(1'b0), .A2(contador_op_1_q0[2]),
    .c(display_hex_11_c), .d(display_hex_11_d), .e(display_hex_11_e), .f(display_hex_11_f),
    .g(display_hex_11_g), .a(display_hex_11_a), .b(display_hex_11_b));
  _7_Segment_Display #(.decimalPoint("false")) A (
    .g(display_hex_9_g), .f(display_hex_9_f), .a(display_hex_9_a), .b(display_hex_9_b), .e(display_hex_9_e),
    .d(display_hex_9_d), .c(display_hex_9_c));
  _7_Segment_Display #(.decimalPoint("false")) B (
    .g(display_hex_10_g), .f(display_hex_10_f), .a(display_hex_10_a), .b(display_hex_10_b),
    .e(display_hex_10_e), .d(display_hex_10_d), .c(display_hex_10_c));
  _7_Segment_Display #(.decimalPoint("false")) OPERACAO (
    .g(display_hex_11_g), .f(display_hex_11_f), .a(display_hex_11_a), .b(display_hex_11_b),
    .e(display_hex_11_e), .d(display_hex_11_d), .c(display_hex_11_c));
  ULA ula_1 (
    .OP(contador_op_1_q0), .ON_OFF(ON_OFF), .A({A3, A2, A1, A0}), .B({B3, B2, B1, B0}), .S(ula_1_s),
    .DOISBITS(ula_1_doisbits));
  xor xor_1 (xor_1_out, ON_OFF, ula_1_doisbits);
  _7_Segment_Display u_7_segment_display_9 (
    .g(display1_6_g), .f(display1_6_f), .a(display1_6_a), .b(display1_6_b), .e(display1_6_e),
    .d(display1_6_d), .c(display1_6_c));  // open: dp
  _7_Segment_Display u_7_segment_display_10 (
    .g(display1_5_g), .f(display1_5_f), .a(display1_5_a), .b(display1_5_b), .e(display1_5_e),
    .d(display1_5_d), .c(display1_5_c));  // open: dp
  _7_Segment_Display u_7_segment_display_11 (
    .g(display1_2_g), .f(display1_2_f), .a(display1_2_a), .b(display1_2_b), .e(display1_2_e),
    .d(display1_2_d), .c(display1_2_c));  // open: dp
  _7_Segment_Display u_7_segment_display_12 (
    .g(display1_4_g), .f(display1_4_f), .a(display1_4_a), .b(display1_4_b), .e(display1_4_e),
    .d(display1_4_d), .c(display1_4_c));  // open: dp
  DISPLAY4 display4_1 (
    .a3(ula_1_s[3]), .a2(ula_1_s[2]), .a1(ula_1_s[1]), .a0(ula_1_s[0]), .ON_OFF(xor_1_out), .a(display4_1_a),
    .b(display4_1_b), .c(display4_1_c), .d(display4_1_d), .e(display4_1_e), .f(display4_1_f), .g(display4_1_g));
  _7_Segment_Display S_HEX (
    .g(display4_1_g), .f(display4_1_f), .a(display4_1_a), .b(display4_1_b), .e(display4_1_e),
    .d(display4_1_d), .c(display4_1_c));  // open: dp
  _7_Segment_Display u_7_segment_display_13 (
    .g(display1_3_g), .f(display1_3_f), .a(display1_3_a), .b(display1_3_b), .e(display1_3_e),
    .d(display1_3_d), .c(display1_3_c));  // open: dp
  DISPLAY1 display1_1 (
    .a0(ula_1_s[0]), .ON_OFF(ON_OFF), .a(display1_1_a), .b(display1_1_b), .c(display1_1_c), .d(display1_1_d),
    .e(display1_1_e), .f(display1_1_f), .g(display1_1_g));
  _7_Segment_Display S_BIN (
    .g(display1_1_g), .f(display1_1_f), .a(display1_1_a), .b(display1_1_b), .e(display1_1_e),
    .d(display1_1_d), .c(display1_1_c));  // open: dp
  DISPLAY1 display1_2 (
    .a0(ula_1_s[4]), .ON_OFF(xor_1_out), .a(display1_2_a), .b(display1_2_b), .c(display1_2_c),
    .d(display1_2_d), .e(display1_2_e), .f(display1_2_f), .g(display1_2_g));
  DISPLAY1 display1_3 (
    .a0(ula_1_s[1]), .ON_OFF(ON_OFF), .a(display1_3_a), .b(display1_3_b), .c(display1_3_c), .d(display1_3_d),
    .e(display1_3_e), .f(display1_3_f), .g(display1_3_g));
  DISPLAY1 display1_4 (
    .a0(ula_1_s[2]), .ON_OFF(ON_OFF), .a(display1_4_a), .b(display1_4_b), .c(display1_4_c), .d(display1_4_d),
    .e(display1_4_e), .f(display1_4_f), .g(display1_4_g));
  _7_Segment_Display u_7_segment_display_14 (
    .g(display5_decimal_bit_mais_sign_1_g), .f(display5_decimal_bit_mais_sign_1_f),
    .a(display5_decimal_bit_mais_sign_1_a), .b(display5_decimal_bit_mais_sign_1_b),
    .e(display5_decimal_bit_mais_sign_1_e), .d(display5_decimal_bit_mais_sign_1_d),
    .c(display5_decimal_bit_mais_sign_1_c));  // open: dp
  DISPLAY5_DECIMAL display5_decimal_1 (
    .ON_OFF(xor_1_out), .a4(ula_1_s[4]), .a3(ula_1_s[3]), .a2(ula_1_s[2]), .a1(ula_1_s[1]), .a0(ula_1_s[0]),
    .a(display5_decimal_1_a), .b(display5_decimal_1_b), .c(display5_decimal_1_c), .d(display5_decimal_1_d),
    .e(display5_decimal_1_e), .f(display5_decimal_1_f), .g(display5_decimal_1_g));
  _7_Segment_Display S_DEC (
    .g(display5_decimal_1_g), .f(display5_decimal_1_f), .a(display5_decimal_1_a), .b(display5_decimal_1_b),
    .e(display5_decimal_1_e), .d(display5_decimal_1_d), .c(display5_decimal_1_c));  // open: dp
  DISPLAY1 display1_5 (
    .a0(ula_1_s[3]), .ON_OFF(ON_OFF), .a(display1_5_a), .b(display1_5_b), .c(display1_5_c), .d(display1_5_d),
    .e(display1_5_e), .f(display1_5_f), .g(display1_5_g));
  xor xor_2 (xor_2_out, ON_OFF, ula_1_doisbits);
  DISPLAY5_DECIMAL_BIT_MAIS_SIGN display5_decimal_bit_mais_sign_1 (
    .ON_OFF(xor_1_out), .a4(ula_1_s[4]), .a3(ula_1_s[3]), .a2(ula_1_s[2]), .a1(ula_1_s[1]), .a0(ula_1_s[0]),
    .a(display5_decimal_bit_mais_sign_1_a), .b(display5_decimal_bit_mais_sign_1_b),
    .c(display5_decimal_bit_mais_sign_1_c), .d(display5_decimal_bit_mais_sign_1_d),
    .e(display5_decimal_bit_mais_sign_1_e), .f(display5_decimal_bit_mais_sign_1_f),
    .g(display5_decimal_bit_mais_sign_1_g));
  DISPLAY1 display1_6 (
    .a0(ula_1_s[4]), .ON_OFF(xor_2_out), .a(display1_6_a), .b(display1_6_b), .c(display1_6_c),
    .d(display1_6_d), .e(display1_6_e), .f(display1_6_f), .g(display1_6_g));

  // Other names for the same wires on the sheet: C = CLEAR; L = LOAD; P = PRESET

  // Notes on the sheet:
  //   0 - SOMA
  //   1 - SUBTRAÇÃO
  //   2 - SUBTRAÇÃO COMPLEMENTO DE 2
  //   3 - AND
  //   4 - OR
  //   5 - NOT A
  //   6 - COMPLEMENTO DE 2 DE A
  //   7 - COMPARADOR A B (EXTRA)
  //   A
  //   C
  //   A
  //   D
  //   9
  //   1
  //   A
  //   8
  //   F
  //   OPERAÇÕES
  //   B
  //   0
  //   5
  //   A
  //   9
  //   4
  //   F
  //   5
  //   8
  //   OPERAÇÃO
  //   5
  //   0
  //   1
  //   7
  //   7
  //   0
  //   5
  //   4
endmodule

module ULA (
  input  ON_OFF,
  input  [2:0] OP,
  input  [3:0] A,
  input  [3:0] B,
  output [4:0] S,
  output DOISBITS
);

  wire demux_1_8_1_o0, demux_1_8_1_o1, demux_1_8_1_o2, display1_1_a, display1_1_b, display1_1_c,
       display1_1_d, display1_1_e, display1_1_f, display1_1_g, display1_2_a, display1_2_b, display1_2_c,
       display1_2_d, display1_2_e, display1_2_f, display1_2_g, display1_3_a, display1_3_b, display1_3_c,
       display1_3_d, display1_3_e, display1_3_f, display1_3_g, display1_4_a, display1_4_b, display1_4_c,
       display1_4_d, display1_4_e, display1_4_f, display1_4_g, display1_5_a, display1_5_b, display1_5_c,
       display1_5_d, display1_5_e, display1_5_f, display1_5_g, display1_6_a, display1_6_b, display1_6_c,
       display1_6_d, display1_6_e, display1_6_f, display1_6_g, display4_1_a, display4_1_b, display4_1_c,
       display4_1_d, display4_1_e, display4_1_f, display4_1_g, display4_2_a, display4_2_b, display4_2_c,
       display4_2_d, display4_2_e, display4_2_f, display4_2_g, display4_3_a, display4_3_b, display4_3_c,
       display4_3_d, display4_3_e, display4_3_f, display4_3_g, display4_4_a, display4_4_b, display4_4_c,
       display4_4_d, display4_4_e, display4_4_f, display4_4_g, or_8_out, or_9_out, or_10_out, xor_1_out,
       xor_2_out;
  wire [3:0] subtrator_4_comp2_1_s0;
  wire [4:0] and_a_b_1_s0, comparador_a_b_1_s0, complemento_2_1_s0, not_a_1_s0, or_1_out, or_2_out, or_3_out,
       or_4_out, or_5_out, or_6_out, or_a_b_1_s0, somador_4_1_s0, subtrator_4_1_s0;

  DEMUX_1_8 demux_1_8_1 (
    .E(ON_OFF), .S2(OP[2]), .S1(OP[1]), .S0(OP[0]), .O0(demux_1_8_1_o0), .O1(demux_1_8_1_o1),
    .O2(demux_1_8_1_o2), .O3(and_a_b_1_s0[4]), .O4(or_a_b_1_s0[4]), .O5(not_a_1_s0[4]),
    .O6(complemento_2_1_s0[4]), .O7(comparador_a_b_1_s0[4]));
  DISPLAY4 display4_1 (
    .a3(A[3]), .a2(A[2]), .a1(A[1]), .a0(A[0]), .ON_OFF(ON_OFF), .a(display4_1_a), .b(display4_1_b),
    .c(display4_1_c), .d(display4_1_d), .e(display4_1_e), .f(display4_1_f), .g(display4_1_g));
  _7_Segment_Display A_HEX (
    .g(display4_1_g), .f(display4_1_f), .a(display4_1_a), .b(display4_1_b), .e(display4_1_e),
    .d(display4_1_d), .c(display4_1_c));  // open: dp
  SOMADOR_4 somador_4_1 (
    .A3(A[3]), .A2(A[2]), .A1(A[1]), .A0(A[0]), .ON_OFF(demux_1_8_1_o0), .B3(B[3]), .B2(B[2]), .B1(B[1]),
    .B0(B[0]), .S4(somador_4_1_s0[4]), .S3(somador_4_1_s0[3]), .S2(somador_4_1_s0[2]),
    .S1(somador_4_1_s0[1]), .S0(somador_4_1_s0[0]));
  SUBTRATOR_4 subtrator_4_1 (
    .A3(A[3]), .A2(A[2]), .A1(A[1]), .A0(A[0]), .ON_OFF(demux_1_8_1_o1), .B3(B[3]), .B2(B[2]), .B1(B[1]),
    .B0(B[0]), .S4(subtrator_4_1_s0[4]), .S3(subtrator_4_1_s0[3]), .S2(subtrator_4_1_s0[2]),
    .S1(subtrator_4_1_s0[1]), .S0(subtrator_4_1_s0[0]));
  SUBTRATOR_4_COMP2 subtrator_4_comp2_1 (
    .A3(A[3]), .A2(A[2]), .A1(A[1]), .A0(A[0]), .ON_OFF(demux_1_8_1_o2), .B3(B[3]), .B2(B[2]), .B1(B[1]),
    .B0(B[0]), .S3(subtrator_4_comp2_1_s0[3]), .S2(subtrator_4_comp2_1_s0[2]),
    .S1(subtrator_4_comp2_1_s0[1]), .S0(subtrator_4_comp2_1_s0[0]));
  AND_A_B and_a_b_1 (
    .ON_OFF(and_a_b_1_s0[4]), .A3(A[3]), .A2(A[2]), .A1(A[1]), .A0(A[0]), .B3(B[3]), .B2(B[2]), .B1(B[1]),
    .B0(B[0]), .S3(and_a_b_1_s0[3]), .S2(and_a_b_1_s0[2]), .S1(and_a_b_1_s0[1]), .S0(and_a_b_1_s0[0]));
  OR_A_B or_a_b_1 (
    .ON_OFF(or_a_b_1_s0[4]), .A3(A[3]), .A2(A[2]), .A1(A[1]), .A0(A[0]), .B3(B[3]), .B2(B[2]), .B1(B[1]),
    .B0(B[0]), .S3(or_a_b_1_s0[3]), .S2(or_a_b_1_s0[2]), .S1(or_a_b_1_s0[1]), .S0(or_a_b_1_s0[0]));
  NOT_A not_a_1 (
    .ON_OFF(not_a_1_s0[4]), .A3(A[3]), .A2(A[2]), .A1(A[1]), .A0(A[0]), .S3(not_a_1_s0[3]),
    .S2(not_a_1_s0[2]), .S1(not_a_1_s0[1]), .S0(not_a_1_s0[0]));
  COMPLEMENTO_2 complemento_2_1 (
    .ON_OFF(complemento_2_1_s0[4]), .A3(A[3]), .A2(A[2]), .A1(A[1]), .A0(A[0]), .S3(complemento_2_1_s0[3]),
    .S2(complemento_2_1_s0[2]), .S1(complemento_2_1_s0[1]), .S0(complemento_2_1_s0[0]));
  COMPARADOR_A_B comparador_a_b_1 (
    .ON_OFF(comparador_a_b_1_s0[4]), .A3(A[3]), .A2(A[2]), .A1(A[1]), .A0(A[0]), .B3(B[3]), .B2(B[2]),
    .B1(B[1]), .B0(B[0]), .S3(comparador_a_b_1_s0[3]), .S2(comparador_a_b_1_s0[2]),
    .S1(comparador_a_b_1_s0[1]), .S0(comparador_a_b_1_s0[0]));
  assign or_1_out = somador_4_1_s0 | subtrator_4_1_s0;  // OR_Gate or_1, 5 bits wide
  assign or_2_out = or_1_out | {1'b0, subtrator_4_comp2_1_s0};  // OR_Gate or_2, 5 bits wide
  assign or_3_out = or_2_out | and_a_b_1_s0;  // OR_Gate or_3, 5 bits wide
  assign or_4_out = or_3_out | or_a_b_1_s0;  // OR_Gate or_4, 5 bits wide
  DISPLAY4 display4_2 (
    .a3(1'b0), .a2(OP[2]), .a1(OP[1]), .a0(OP[0]), .ON_OFF(ON_OFF), .a(display4_2_a), .b(display4_2_b),
    .c(display4_2_c), .d(display4_2_d), .e(display4_2_e), .f(display4_2_f), .g(display4_2_g));
  _7_Segment_Display OPERATOR (
    .g(display4_2_g), .f(display4_2_f), .a(display4_2_a), .b(display4_2_b), .e(display4_2_e),
    .d(display4_2_d), .c(display4_2_c));  // open: dp
  assign or_5_out = or_4_out | not_a_1_s0;  // OR_Gate or_5, 5 bits wide
  assign or_6_out = or_5_out | complemento_2_1_s0;  // OR_Gate or_6, 5 bits wide
  assign S = or_6_out | comparador_a_b_1_s0;  // OR_Gate or_7, 5 bits wide
  _7_Segment_Display S_BIN4 (
    .g(display1_6_g), .f(display1_6_f), .a(display1_6_a), .b(display1_6_b), .e(display1_6_e),
    .d(display1_6_d), .c(display1_6_c));  // open: dp
  or or_8 (or_8_out, and_a_b_1_s0[4], or_a_b_1_s0[4]);
  or or_9 (or_9_out, or_8_out, not_a_1_s0[4]);
  xor xor_1 (xor_1_out, DOISBITS, ON_OFF);
  _7_Segment_Display S_BIN3 (
    .g(display1_5_g), .f(display1_5_f), .a(display1_5_a), .b(display1_5_b), .e(display1_5_e),
    .d(display1_5_d), .c(display1_5_c));  // open: dp
  or or_10 (or_10_out, or_9_out, complemento_2_1_s0[4]);
  or or_11 (DOISBITS, or_10_out, comparador_a_b_1_s0[4]);
  DISPLAY4 display4_3 (
    .a3(B[3]), .a2(B[2]), .a1(B[1]), .a0(B[0]), .ON_OFF(ON_OFF), .a(display4_3_a), .b(display4_3_b),
    .c(display4_3_c), .d(display4_3_d), .e(display4_3_e), .f(display4_3_f), .g(display4_3_g));
  _7_Segment_Display B_HEX (
    .g(display4_3_g), .f(display4_3_f), .a(display4_3_a), .b(display4_3_b), .e(display4_3_e),
    .d(display4_3_d), .c(display4_3_c));  // open: dp
  _7_Segment_Display S_BIN2 (
    .g(display1_4_g), .f(display1_4_f), .a(display1_4_a), .b(display1_4_b), .e(display1_4_e),
    .d(display1_4_d), .c(display1_4_c));  // open: dp
  _7_Segment_Display S_HEX2 (
    .g(display1_2_g), .f(display1_2_f), .a(display1_2_a), .b(display1_2_b), .e(display1_2_e),
    .d(display1_2_d), .c(display1_2_c));  // open: dp
  _7_Segment_Display S_BIN1 (
    .g(display1_3_g), .f(display1_3_f), .a(display1_3_a), .b(display1_3_b), .e(display1_3_e),
    .d(display1_3_d), .c(display1_3_c));  // open: dp
  DISPLAY4 display4_4 (
    .a3(S[3]), .a2(S[2]), .a1(S[1]), .a0(S[0]), .ON_OFF(xor_1_out), .a(display4_4_a), .b(display4_4_b),
    .c(display4_4_c), .d(display4_4_d), .e(display4_4_e), .f(display4_4_f), .g(display4_4_g));
  _7_Segment_Display S_HEX (
    .g(display4_4_g), .f(display4_4_f), .a(display4_4_a), .b(display4_4_b), .e(display4_4_e),
    .d(display4_4_d), .c(display4_4_c));  // open: dp
  DISPLAY1 display1_1 (
    .a0(S[0]), .ON_OFF(ON_OFF), .a(display1_1_a), .b(display1_1_b), .c(display1_1_c), .d(display1_1_d),
    .e(display1_1_e), .f(display1_1_f), .g(display1_1_g));
  _7_Segment_Display S_BIN (
    .g(display1_1_g), .f(display1_1_f), .a(display1_1_a), .b(display1_1_b), .e(display1_1_e),
    .d(display1_1_d), .c(display1_1_c));  // open: dp
  DISPLAY1 display1_2 (
    .a0(S[4]), .ON_OFF(xor_1_out), .a(display1_2_a), .b(display1_2_b), .c(display1_2_c), .d(display1_2_d),
    .e(display1_2_e), .f(display1_2_f), .g(display1_2_g));
  DISPLAY1 display1_3 (
    .a0(S[1]), .ON_OFF(ON_OFF), .a(display1_3_a), .b(display1_3_b), .c(display1_3_c), .d(display1_3_d),
    .e(display1_3_e), .f(display1_3_f), .g(display1_3_g));
  DISPLAY1 display1_4 (
    .a0(S[2]), .ON_OFF(ON_OFF), .a(display1_4_a), .b(display1_4_b), .c(display1_4_c), .d(display1_4_d),
    .e(display1_4_e), .f(display1_4_f), .g(display1_4_g));
  xor xor_2 (xor_2_out, ON_OFF, DOISBITS);
  DISPLAY1 display1_5 (
    .a0(S[3]), .ON_OFF(ON_OFF), .a(display1_5_a), .b(display1_5_b), .c(display1_5_c), .d(display1_5_d),
    .e(display1_5_e), .f(display1_5_f), .g(display1_5_g));
  DISPLAY1 display1_6 (
    .a0(S[4]), .ON_OFF(xor_2_out), .a(display1_6_a), .b(display1_6_b), .c(display1_6_c), .d(display1_6_d),
    .e(display1_6_e), .f(display1_6_f), .g(display1_6_g));
endmodule

module CONTADOR_OP (
  input  PRESET,
  input  CLK,
  input  CLEAR,
  input  LOAD,
  output Q0,
  output Q1,
  output Q2
);

  wire C0, C1, C2, CAUX, display_hex_1_a, display_hex_1_b, display_hex_1_c, display_hex_1_d, display_hex_1_e,
       display_hex_1_f, display_hex_1_g, or_1_out, or_2_out, or_3_out, or_4_out, or_5_out, or_6_out,
       or_7_out, or_8_out, P0, P1, P2, PAUX, QAUX;
  wire [1:0] combinacional_op_1_j0, combinacional_op_1_j1, combinacional_op_1_j2, combinacional_op_1_jaux;

  or or_1 (or_1_out, PRESET, P0);
  FF_JK_MS_SR ff_jk_ms_sr_1 (
    .J(combinacional_op_1_j0[0]), .CLK(CLK), .K(combinacional_op_1_j0[1]), .PRESET(or_1_out),
    .CLEAR(or_2_out), .Q(Q0));  // open: nQ
  or or_2 (or_2_out, CLEAR, C0);
  or or_3 (or_3_out, PRESET, P1);
  FF_JK_MS_SR ff_jk_ms_sr_2 (
    .J(combinacional_op_1_j1[0]), .CLK(CLK), .K(combinacional_op_1_j1[1]), .PRESET(or_3_out),
    .CLEAR(or_4_out), .Q(Q1));  // open: nQ
  or or_4 (or_4_out, CLEAR, C1);
  COMBINACIONAL_OP combinacional_op_1 (
    .A1(Q1), .A0(Q0), .AUX(QAUX), .A2(Q2), .J2(combinacional_op_1_j2[0]), .K2(combinacional_op_1_j2[1]),
    .J1(combinacional_op_1_j1[0]), .K1(combinacional_op_1_j1[1]), .J0(combinacional_op_1_j0[0]),
    .K0(combinacional_op_1_j0[1]), .JAUX(combinacional_op_1_jaux[0]), .KAUX(combinacional_op_1_jaux[1]));
  or or_5 (or_5_out, PRESET, P2);
  or or_6 (or_6_out, CLEAR, C2);
  FF_JK_MS_SR ff_jk_ms_sr_3 (
    .J(combinacional_op_1_j2[0]), .CLK(CLK), .K(combinacional_op_1_j2[1]), .PRESET(or_5_out),
    .CLEAR(or_6_out), .Q(Q2));  // open: nQ
  or or_7 (or_7_out, PRESET, PAUX);
  FF_JK_MS_SR ff_jk_ms_sr_4 (
    .J(combinacional_op_1_jaux[0]), .CLK(CLK), .K(combinacional_op_1_jaux[1]), .PRESET(or_7_out),
    .CLEAR(or_8_out), .Q(QAUX));  // open: nQ
  or or_8 (or_8_out, CLEAR, CAUX);
  CLEAR_PRESET clear_preset_1 (.E(1'b1), .ENABLE(LOAD), .PRESET(P0), .CLEAR(C0));
  CLEAR_PRESET clear_preset_2 (.E(1'b0), .ENABLE(LOAD), .PRESET(P1), .CLEAR(C1));
  CLEAR_PRESET clear_preset_3 (.E(1'b1), .ENABLE(LOAD), .PRESET(P2), .CLEAR(C2));
  CLEAR_PRESET clear_preset_4 (.E(1'b0), .ENABLE(LOAD), .PRESET(PAUX), .CLEAR(CAUX));
  DISPLAY_HEX display_hex_1 (
    .A1(Q1), .A0(Q0), .A3(1'b0), .A2(Q2), .c(display_hex_1_c), .d(display_hex_1_d), .e(display_hex_1_e),
    .f(display_hex_1_f), .g(display_hex_1_g), .a(display_hex_1_a), .b(display_hex_1_b));
  _7_Segment_Display #(.decimalPoint("false")) u_7_segment_display_1 (
    .g(display_hex_1_g), .f(display_hex_1_f), .a(display_hex_1_a), .b(display_hex_1_b), .e(display_hex_1_e),
    .d(display_hex_1_d), .c(display_hex_1_c));
endmodule

module CONTADOR_1 (
  input  PRESET,
  input  CLK,
  input  CLEAR,
  input  LOAD,
  output Q0,
  output Q1,
  output Q2,
  output Q3
);

  wire C0, C1, C2, C3, CAUX, display_hex_1_a, display_hex_1_b, display_hex_1_c, display_hex_1_d,
       display_hex_1_e, display_hex_1_f, display_hex_1_g, or_1_out, or_2_out, or_3_out, or_4_out, or_5_out,
       or_6_out, or_7_out, or_8_out, or_9_out, or_10_out, P0, P1, P2, P3, PAUX, QAUX;
  wire [1:0] combinacional_1_1_j0, combinacional_1_1_j1, combinacional_1_1_j2, combinacional_1_1_j3,
       combinacional_1_1_jaux;

  or or_1 (or_1_out, PRESET, P0);
  FF_JK_MS_SR ff_jk_ms_sr_1 (
    .J(combinacional_1_1_j0[0]), .CLK(CLK), .K(combinacional_1_1_j0[1]), .PRESET(or_1_out), .CLEAR(or_2_out),
    .Q(Q0));  // open: nQ
  or or_2 (or_2_out, CLEAR, C0);
  or or_3 (or_3_out, PRESET, P1);
  or or_4 (or_4_out, CLEAR, C1);
  FF_JK_MS_SR ff_jk_ms_sr_2 (
    .J(combinacional_1_1_j1[0]), .CLK(CLK), .K(combinacional_1_1_j1[1]), .PRESET(or_3_out), .CLEAR(or_4_out),
    .Q(Q1));  // open: nQ
  COMBINACIONAL_1 combinacional_1_1 (
    .A2(Q2), .A1(Q1), .A0(Q0), .AUX(QAUX), .A3(Q3), .J3(combinacional_1_1_j3[0]),
    .K3(combinacional_1_1_j3[1]), .J2(combinacional_1_1_j2[0]), .K2(combinacional_1_1_j2[1]),
    .J1(combinacional_1_1_j1[0]), .K1(combinacional_1_1_j1[1]), .J0(combinacional_1_1_j0[0]),
    .K0(combinacional_1_1_j0[1]), .JAUX(combinacional_1_1_jaux[0]), .KAUX(combinacional_1_1_jaux[1]));
  or or_5 (or_5_out, PRESET, P2);
  FF_JK_MS_SR ff_jk_ms_sr_3 (
    .J(combinacional_1_1_j2[0]), .CLK(CLK), .K(combinacional_1_1_j2[1]), .PRESET(or_5_out), .CLEAR(or_6_out),
    .Q(Q2));  // open: nQ
  or or_6 (or_6_out, CLEAR, C2);
  or or_7 (or_7_out, PRESET, P3);
  FF_JK_MS_SR ff_jk_ms_sr_4 (
    .J(combinacional_1_1_j3[0]), .CLK(CLK), .K(combinacional_1_1_j3[1]), .PRESET(or_7_out), .CLEAR(or_8_out),
    .Q(Q3));  // open: nQ
  or or_8 (or_8_out, CLEAR, C3);
  or or_9 (or_9_out, PRESET, PAUX);
  FF_JK_MS_SR ff_jk_ms_sr_5 (
    .J(combinacional_1_1_jaux[0]), .CLK(CLK), .K(combinacional_1_1_jaux[1]), .PRESET(or_9_out),
    .CLEAR(or_10_out), .Q(QAUX));  // open: nQ
  or or_10 (or_10_out, CLEAR, CAUX);
  CLEAR_PRESET clear_preset_1 (.E(1'b0), .ENABLE(LOAD), .PRESET(P0), .CLEAR(C0));
  CLEAR_PRESET clear_preset_2 (.E(1'b0), .ENABLE(LOAD), .PRESET(P1), .CLEAR(C1));
  CLEAR_PRESET clear_preset_3 (.E(1'b1), .ENABLE(LOAD), .PRESET(P2), .CLEAR(C2));
  CLEAR_PRESET clear_preset_4 (.E(1'b1), .ENABLE(LOAD), .PRESET(P3), .CLEAR(C3));
  CLEAR_PRESET clear_preset_5 (.E(1'b0), .ENABLE(LOAD), .PRESET(PAUX), .CLEAR(CAUX));
  DISPLAY_HEX display_hex_1 (
    .A1(Q1), .A0(Q0), .A3(Q3), .A2(Q2), .c(display_hex_1_c), .d(display_hex_1_d), .e(display_hex_1_e),
    .f(display_hex_1_f), .g(display_hex_1_g), .a(display_hex_1_a), .b(display_hex_1_b));
  _7_Segment_Display #(.decimalPoint("false")) u_7_segment_display_1 (
    .g(display_hex_1_g), .f(display_hex_1_f), .a(display_hex_1_a), .b(display_hex_1_b), .e(display_hex_1_e),
    .d(display_hex_1_d), .c(display_hex_1_c));
endmodule

module CONTADOR_2 (
  input  PRESET,
  input  CLK,
  input  CLEAR,
  input  LOAD,
  output Q0,
  output Q1,
  output Q2,
  output Q3
);

  wire C0, C1, C2, C3, CAUX, display_hex_1_a, display_hex_1_b, display_hex_1_c, display_hex_1_d,
       display_hex_1_e, display_hex_1_f, display_hex_1_g, or_1_out, or_2_out, or_3_out, or_4_out, or_5_out,
       or_6_out, or_7_out, or_8_out, or_9_out, or_10_out, P0, P1, P2, P3, PAUX, QAUX;
  wire [1:0] combinacional_2_1_j0, combinacional_2_1_j1, combinacional_2_1_j2, combinacional_2_1_j3,
       combinacional_2_1_jaux;

  or or_1 (or_1_out, PRESET, P0);
  FF_JK_MS_SR ff_jk_ms_sr_1 (
    .J(combinacional_2_1_j0[0]), .CLK(CLK), .K(combinacional_2_1_j0[1]), .PRESET(or_1_out), .CLEAR(or_2_out),
    .Q(Q0));  // open: nQ
  or or_2 (or_2_out, CLEAR, C0);
  or or_3 (or_3_out, PRESET, P1);
  or or_4 (or_4_out, CLEAR, C1);
  FF_JK_MS_SR ff_jk_ms_sr_2 (
    .J(combinacional_2_1_j1[0]), .CLK(CLK), .K(combinacional_2_1_j1[1]), .PRESET(or_3_out), .CLEAR(or_4_out),
    .Q(Q1));  // open: nQ
  COMBINACIONAL_2 combinacional_2_1 (
    .A2(Q2), .A1(Q1), .A0(Q0), .AUX(QAUX), .A3(Q3), .J3(combinacional_2_1_j3[0]),
    .K3(combinacional_2_1_j3[1]), .J2(combinacional_2_1_j2[0]), .K2(combinacional_2_1_j2[1]),
    .J1(combinacional_2_1_j1[0]), .K1(combinacional_2_1_j1[1]), .J0(combinacional_2_1_j0[0]),
    .K0(combinacional_2_1_j0[1]), .JAUX(combinacional_2_1_jaux[0]), .KAUX(combinacional_2_1_jaux[1]));
  or or_5 (or_5_out, PRESET, P2);
  FF_JK_MS_SR ff_jk_ms_sr_3 (
    .J(combinacional_2_1_j2[0]), .CLK(CLK), .K(combinacional_2_1_j2[1]), .PRESET(or_5_out), .CLEAR(or_6_out),
    .Q(Q2));  // open: nQ
  or or_6 (or_6_out, CLEAR, C2);
  or or_7 (or_7_out, PRESET, P3);
  FF_JK_MS_SR ff_jk_ms_sr_4 (
    .J(combinacional_2_1_j3[0]), .CLK(CLK), .K(combinacional_2_1_j3[1]), .PRESET(or_7_out), .CLEAR(or_8_out),
    .Q(Q3));  // open: nQ
  or or_8 (or_8_out, CLEAR, C3);
  or or_9 (or_9_out, PRESET, PAUX);
  FF_JK_MS_SR ff_jk_ms_sr_5 (
    .J(combinacional_2_1_jaux[0]), .CLK(CLK), .K(combinacional_2_1_jaux[1]), .PRESET(or_9_out),
    .CLEAR(or_10_out), .Q(QAUX));  // open: nQ
  or or_10 (or_10_out, CLEAR, CAUX);
  CLEAR_PRESET clear_preset_1 (.E(1'b0), .ENABLE(LOAD), .PRESET(P0), .CLEAR(C0));
  CLEAR_PRESET clear_preset_2 (.E(1'b0), .ENABLE(LOAD), .PRESET(P1), .CLEAR(C1));
  CLEAR_PRESET clear_preset_3 (.E(1'b0), .ENABLE(LOAD), .PRESET(P2), .CLEAR(C2));
  CLEAR_PRESET clear_preset_4 (.E(1'b0), .ENABLE(LOAD), .PRESET(P3), .CLEAR(C3));
  CLEAR_PRESET clear_preset_5 (.E(1'b0), .ENABLE(LOAD), .PRESET(PAUX), .CLEAR(CAUX));
  DISPLAY_HEX display_hex_1 (
    .A1(Q1), .A0(Q0), .A3(Q3), .A2(Q2), .c(display_hex_1_c), .d(display_hex_1_d), .e(display_hex_1_e),
    .f(display_hex_1_f), .g(display_hex_1_g), .a(display_hex_1_a), .b(display_hex_1_b));
  _7_Segment_Display #(.decimalPoint("false")) u_7_segment_display_1 (
    .g(display_hex_1_g), .f(display_hex_1_f), .a(display_hex_1_a), .b(display_hex_1_b), .e(display_hex_1_e),
    .d(display_hex_1_d), .c(display_hex_1_c));
endmodule

module COMBINACIONAL_OP (
  input  AUX,
  input  A2,
  input  A1,
  input  A0,
  output JAUX,
  output KAUX,
  output J2,
  output K2,
  output J1,
  output K1,
  output J0,
  output K0
);

  wire and_1_out, and_2_out, and_3_out, and_4_out, and_5_out, and_6_out, and_7_out, and_8_out, and_9_out,
       and_10_out, and_11_out, and_12_out, and_13_out, and_14_out, and_15_out, and_16_out, and_17_out,
       and_18_out, and_19_out, and_20_out, and_21_out, and_22_out, and_23_out, and_24_out, and_25_out,
       and_26_out, and_27_out, and_28_out, and_29_out, and_30_out, and_31_out, and_32_out, and_33_out,
       and_34_out, and_35_out, and_36_out, and_37_out, and_38_out, and_39_out, and_40_out, and_41_out,
       and_42_out, and_43_out, and_44_out, and_45_out, and_46_out, and_47_out, and_48_out, and_49_out,
       and_50_out, and_51_out, and_52_out, and_53_out, and_54_out, and_55_out, and_56_out, and_57_out,
       and_58_out, and_59_out, and_60_out, and_61_out, and_62_out, and_63_out, and_64_out, not_1_out,
       not_2_out, not_3_out, not_4_out, or_3_out, or_4_out, or_5_out, or_6_out, or_7_out, or_8_out, or_9_out,
       or_10_out, or_11_out, or_12_out, or_13_out, or_14_out, or_15_out, or_16_out, or_19_out, or_20_out,
       or_21_out, or_22_out;

  not not_1 (not_1_out, AUX);
  not not_2 (not_2_out, A2);
  not not_3 (not_3_out, A1);
  not not_4 (not_4_out, A0);
  and and_1 (and_1_out, not_1_out, A2);
  and and_2 (and_2_out, AUX, A2);
  and and_3 (and_3_out, not_1_out, A2);
  and and_4 (and_4_out, AUX, A2);
  and and_5 (and_5_out, not_1_out, not_3_out);
  and and_6 (and_6_out, not_1_out, A2);
  and and_7 (and_7_out, A1, not_4_out);
  and and_8 (and_8_out, not_1_out, not_3_out);
  and and_9 (and_9_out, not_1_out, A2);
  and and_10 (and_10_out, A1, not_4_out);
  and and_11 (and_11_out, not_1_out, not_2_out);
  and and_12 (and_12_out, not_1_out, A2);
  and and_13 (and_13_out, not_2_out, not_3_out);
  and and_14 (and_14_out, AUX, A2);
  and and_15 (and_15_out, not_1_out, not_2_out);
  and and_16 (and_16_out, not_1_out, A2);
  and and_17 (and_17_out, not_2_out, not_3_out);
  and and_18 (and_18_out, AUX, A2);
  and and_19 (and_19_out, not_1_out, A1);
  and and_20 (and_20_out, not_1_out, A1);
  and and_21 (and_21_out, and_1_out, A1);
  and and_22 (and_22_out, and_2_out, not_4_out);
  and and_23 (and_23_out, and_3_out, A1);
  and and_24 (and_24_out, and_4_out, not_4_out);
  and and_25 (and_25_out, and_5_out, A0);
  and and_26 (and_26_out, and_6_out, and_7_out);
  and and_27 (and_27_out, AUX, not_2_out);
  and and_28 (and_28_out, not_3_out, not_4_out);
  and and_29 (and_29_out, AUX, A1);
  and and_30 (and_30_out, not_1_out, not_2_out);
  and and_31 (and_31_out, and_8_out, A0);
  and and_32 (and_32_out, and_9_out, and_10_out);
  and and_33 (and_33_out, AUX, not_2_out);
  and and_34 (and_34_out, not_3_out, not_4_out);
  and and_35 (and_35_out, AUX, A1);
  and and_36 (and_36_out, not_1_out, not_2_out);
  and and_37 (and_37_out, and_11_out, A0);
  and and_38 (and_38_out, and_12_out, not_4_out);
  and and_39 (and_39_out, and_13_out, A0);
  and and_40 (and_40_out, and_14_out, A1);
  and and_41 (and_41_out, and_15_out, A0);
  and and_42 (and_42_out, and_16_out, not_4_out);
  and and_43 (and_43_out, and_17_out, A0);
  and and_44 (and_44_out, and_18_out, A1);
  and and_45 (and_45_out, not_2_out, not_4_out);
  and and_46 (and_46_out, not_2_out, A1);
  and and_47 (and_47_out, A2, not_3_out);
  and and_48 (and_48_out, and_19_out, not_4_out);
  and and_49 (and_49_out, AUX, not_3_out);
  and and_50 (and_50_out, not_2_out, not_4_out);
  and and_51 (and_51_out, not_2_out, A1);
  and and_52 (and_52_out, A2, not_3_out);
  and and_53 (and_53_out, and_20_out, not_4_out);
  and and_54 (and_54_out, AUX, not_3_out);
  or or_1 (JAUX, and_21_out, and_22_out);
  or or_2 (KAUX, and_23_out, and_24_out);
  or or_3 (or_3_out, and_25_out, and_26_out);
  and and_55 (and_55_out, and_27_out, and_28_out);
  and and_56 (and_56_out, and_29_out, A0);
  and and_57 (and_57_out, and_30_out, A0);
  or or_4 (or_4_out, and_31_out, and_32_out);
  and and_58 (and_58_out, and_33_out, and_34_out);
  and and_59 (and_59_out, and_35_out, A0);
  and and_60 (and_60_out, and_36_out, A0);
  or or_5 (or_5_out, and_37_out, and_38_out);
  or or_6 (or_6_out, and_39_out, and_40_out);
  or or_7 (or_7_out, and_41_out, and_42_out);
  or or_8 (or_8_out, and_43_out, and_44_out);
  or or_9 (or_9_out, and_45_out, and_46_out);
  and and_61 (and_61_out, and_47_out, A0);
  or or_10 (or_10_out, and_48_out, and_49_out);
  and and_62 (and_62_out, AUX, A0);
  or or_11 (or_11_out, and_50_out, and_51_out);
  and and_63 (and_63_out, and_52_out, A0);
  or or_12 (or_12_out, and_53_out, and_54_out);
  and and_64 (and_64_out, AUX, A0);
  or or_13 (or_13_out, or_3_out, and_55_out);
  or or_14 (or_14_out, and_56_out, and_57_out);
  or or_15 (or_15_out, or_4_out, and_58_out);
  or or_16 (or_16_out, and_59_out, and_60_out);
  or or_17 (J1, or_5_out, or_6_out);
  or or_18 (K1, or_7_out, or_8_out);
  or or_19 (or_19_out, or_9_out, and_61_out);
  or or_20 (or_20_out, or_10_out, and_62_out);
  or or_21 (or_21_out, or_11_out, and_63_out);
  or or_22 (or_22_out, or_12_out, and_64_out);
  or or_23 (J2, or_13_out, or_14_out);
  or or_24 (K2, or_15_out, or_16_out);
  or or_25 (J0, or_19_out, or_20_out);
  or or_26 (K0, or_21_out, or_22_out);
endmodule

module COMBINACIONAL_1 (
  input  AUX,
  input  A3,
  input  A2,
  input  A1,
  input  A0,
  output JAUX,
  output KAUX,
  output J3,
  output K3,
  output J2,
  output K2,
  output J1,
  output K1,
  output J0,
  output K0
);

  wire and_1_out, and_2_out, and_3_out, and_4_out, and_5_out, and_6_out, and_7_out, and_8_out, and_9_out,
       and_10_out, and_11_out, and_12_out, and_13_out, and_14_out, and_15_out, and_16_out, and_17_out,
       and_18_out, and_19_out, and_20_out, and_21_out, and_22_out, and_23_out, and_24_out, and_25_out,
       and_26_out, and_27_out, and_28_out, and_29_out, and_30_out, and_31_out, and_32_out, and_33_out,
       and_34_out, and_35_out, and_36_out, and_37_out, and_38_out, and_39_out, and_40_out, and_41_out,
       and_42_out, and_43_out, and_44_out, and_45_out, and_46_out, and_47_out, and_48_out, and_49_out,
       and_50_out, and_51_out, and_52_out, and_53_out, and_54_out, and_55_out, and_56_out, and_57_out,
       and_58_out, and_59_out, and_60_out, and_61_out, and_62_out, and_63_out, and_64_out, and_65_out,
       and_66_out, and_67_out, and_68_out, and_69_out, and_70_out, and_71_out, and_72_out, and_73_out,
       and_74_out, and_75_out, and_76_out, and_77_out, and_78_out, and_79_out, and_80_out, and_81_out,
       and_82_out, and_83_out, and_84_out, and_85_out, and_86_out, and_87_out, and_88_out, and_89_out,
       and_90_out, and_91_out, and_92_out, and_93_out, and_94_out, and_95_out, and_96_out, and_97_out,
       and_98_out, and_99_out, and_100_out, and_101_out, and_102_out, and_103_out, and_104_out, and_105_out,
       and_106_out, and_107_out, and_108_out, and_109_out, and_110_out, and_111_out, and_112_out,
       and_113_out, and_114_out, and_115_out, and_116_out, and_117_out, and_118_out, and_119_out,
       and_120_out, and_121_out, and_122_out, and_123_out, and_124_out, and_125_out, and_126_out,
       and_127_out, and_128_out, and_129_out, and_130_out, and_131_out, and_132_out, and_133_out,
       and_134_out, and_135_out, and_136_out, and_137_out, and_138_out, and_139_out, and_140_out,
       and_141_out, and_142_out, and_143_out, and_144_out, and_145_out, and_146_out, and_147_out,
       and_148_out, not_1_out, not_2_out, not_3_out, not_4_out, not_5_out, or_5_out, or_6_out, or_7_out,
       or_8_out, or_9_out, or_10_out, or_11_out, or_12_out, or_13_out, or_14_out, or_15_out, or_16_out,
       or_17_out, or_18_out, or_19_out, or_20_out, or_21_out, or_22_out, or_23_out, or_24_out, or_25_out,
       or_26_out, or_27_out, or_28_out, or_29_out, or_30_out, or_31_out, or_32_out, or_33_out, or_34_out,
       or_35_out, or_36_out, or_37_out, or_38_out, or_39_out, or_40_out, or_43_out, or_44_out, or_45_out,
       or_46_out, or_47_out, or_48_out, or_49_out, or_50_out;

  not not_1 (not_1_out, AUX);
  not not_2 (not_2_out, A3);
  not not_3 (not_3_out, A2);
  not not_4 (not_4_out, A1);
  not not_5 (not_5_out, A0);
  and and_1 (and_1_out, A3, not_3_out);
  and and_2 (and_2_out, A1, not_5_out);
  and and_3 (and_3_out, AUX, A3);
  and and_4 (and_4_out, A2, A1);
  and and_5 (and_5_out, A3, not_3_out);
  and and_6 (and_6_out, A1, not_5_out);
  and and_7 (and_7_out, AUX, A3);
  and and_8 (and_8_out, A2, A1);
  and and_9 (and_9_out, AUX, not_3_out);
  and and_10 (and_10_out, not_4_out, A0);
  and and_11 (and_11_out, not_2_out, A2);
  and and_12 (and_12_out, A1, A0);
  and and_13 (and_13_out, AUX, not_3_out);
  and and_14 (and_14_out, not_4_out, A0);
  and and_15 (and_15_out, not_2_out, A2);
  and and_16 (and_16_out, A1, A0);
  and and_17 (and_17_out, not_2_out, A1);
  and and_18 (and_18_out, not_3_out, A1);
  and and_19 (and_19_out, AUX, A3);
  and and_20 (and_20_out, not_2_out, A1);
  and and_21 (and_21_out, not_3_out, A1);
  and and_22 (and_22_out, AUX, A3);
  and and_23 (and_23_out, AUX, not_3_out);
  and and_24 (and_24_out, not_4_out, not_5_out);
  and and_25 (and_25_out, AUX, not_3_out);
  and and_26 (and_26_out, not_4_out, not_5_out);
  and and_27 (and_27_out, A3, not_3_out);
  and and_28 (and_28_out, not_4_out, not_5_out);
  and and_29 (and_29_out, not_1_out, not_2_out);
  and and_30 (and_30_out, not_1_out, not_2_out);
  and and_31 (and_31_out, not_1_out, not_2_out);
  and and_32 (and_32_out, not_1_out, not_3_out);
  and and_33 (and_33_out, not_1_out, A2);
  and and_34 (and_34_out, not_4_out, A0);
  and and_35 (and_35_out, not_1_out, A3);
  and and_36 (and_36_out, A2, A0);
  and and_37 (and_37_out, not_2_out, not_3_out);
  and and_38 (and_38_out, not_2_out, not_3_out);
  and and_39 (and_39_out, not_2_out, A2);
  and and_40 (and_40_out, not_2_out, A1);
  and and_41 (and_41_out, AUX, not_2_out);
  and and_42 (and_42_out, A3, not_3_out);
  and and_43 (and_43_out, not_4_out, not_5_out);
  and and_44 (and_44_out, not_1_out, not_2_out);
  and and_45 (and_45_out, not_1_out, not_2_out);
  and and_46 (and_46_out, not_1_out, not_2_out);
  and and_47 (and_47_out, not_1_out, not_3_out);
  and and_48 (and_48_out, not_1_out, A2);
  and and_49 (and_49_out, not_4_out, A0);
  and and_50 (and_50_out, not_1_out, A3);
  and and_51 (and_51_out, A2, A0);
  and and_52 (and_52_out, not_2_out, not_3_out);
  and and_53 (and_53_out, not_2_out, not_3_out);
  and and_54 (and_54_out, not_2_out, A2);
  and and_55 (and_55_out, not_2_out, A1);
  and and_56 (and_56_out, AUX, not_2_out);
  and and_57 (and_57_out, and_1_out, and_2_out);
  and and_58 (and_58_out, and_3_out, and_4_out);
  and and_59 (and_59_out, and_5_out, and_6_out);
  and and_60 (and_60_out, and_7_out, and_8_out);
  and and_61 (and_61_out, and_9_out, and_10_out);
  and and_62 (and_62_out, and_11_out, and_12_out);
  and and_63 (and_63_out, and_13_out, and_14_out);
  and and_64 (and_64_out, and_15_out, and_16_out);
  and and_65 (and_65_out, and_17_out, A0);
  and and_66 (and_66_out, and_18_out, A0);
  and and_67 (and_67_out, not_1_out, A3);
  and and_68 (and_68_out, not_4_out, not_5_out);
  and and_69 (and_69_out, and_19_out, A2);
  and and_70 (and_70_out, not_4_out, A0);
  and and_71 (and_71_out, not_1_out, A3);
  and and_72 (and_72_out, not_3_out, not_5_out);
  and and_73 (and_73_out, and_20_out, A0);
  and and_74 (and_74_out, and_21_out, A0);
  and and_75 (and_75_out, not_1_out, A3);
  and and_76 (and_76_out, not_4_out, not_5_out);
  and and_77 (and_77_out, and_22_out, A2);
  and and_78 (and_78_out, not_4_out, A0);
  and and_79 (and_79_out, not_1_out, A3);
  and and_80 (and_80_out, not_3_out, not_5_out);
  and and_81 (and_81_out, not_2_out, A0);
  and and_82 (and_82_out, and_23_out, and_24_out);
  and and_83 (and_83_out, A3, not_3_out);
  and and_84 (and_84_out, not_1_out, A3);
  and and_85 (and_85_out, A3, not_4_out);
  and and_86 (and_86_out, not_1_out, A3);
  and and_87 (and_87_out, A3, not_3_out);
  and and_88 (and_88_out, AUX, A3);
  and and_89 (and_89_out, not_2_out, A0);
  and and_90 (and_90_out, and_25_out, and_26_out);
  and and_91 (and_91_out, A3, not_3_out);
  and and_92 (and_92_out, not_1_out, A3);
  and and_93 (and_93_out, A3, not_4_out);
  and and_94 (and_94_out, not_1_out, A3);
  and and_95 (and_95_out, A3, not_3_out);
  and and_96 (and_96_out, AUX, A3);
  and and_97 (and_97_out, and_27_out, and_28_out);
  and and_98 (and_98_out, and_29_out, not_3_out);
  and and_99 (and_99_out, and_30_out, not_4_out);
  and and_100 (and_100_out, and_31_out, not_5_out);
  and and_101 (and_101_out, and_32_out, not_5_out);
  and and_102 (and_102_out, and_33_out, and_34_out);
  and and_103 (and_103_out, not_1_out, A1);
  and and_104 (and_104_out, and_35_out, and_36_out);
  and and_105 (and_105_out, and_37_out, A0);
  and and_106 (and_106_out, and_38_out, A1);
  and and_107 (and_107_out, and_39_out, not_4_out);
  and and_108 (and_108_out, and_40_out, not_5_out);
  and and_109 (and_109_out, and_41_out, A0);
  and and_110 (and_110_out, AUX, A1);
  and and_111 (and_111_out, and_42_out, and_43_out);
  and and_112 (and_112_out, and_44_out, not_3_out);
  and and_113 (and_113_out, and_45_out, not_4_out);
  and and_114 (and_114_out, and_46_out, not_5_out);
  and and_115 (and_115_out, and_47_out, not_5_out);
  and and_116 (and_116_out, and_48_out, and_49_out);
  and and_117 (and_117_out, not_1_out, A1);
  and and_118 (and_118_out, and_50_out, and_51_out);
  and and_119 (and_119_out, and_52_out, A0);
  and and_120 (and_120_out, and_53_out, A1);
  and and_121 (and_121_out, and_54_out, not_4_out);
  and and_122 (and_122_out, and_55_out, not_5_out);
  and and_123 (and_123_out, and_56_out, A0);
  and and_124 (and_124_out, AUX, A1);
  or or_1 (JAUX, and_57_out, and_58_out);
  or or_2 (KAUX, and_59_out, and_60_out);
  or or_3 (J3, and_61_out, and_62_out);
  or or_4 (K3, and_63_out, and_64_out);
  or or_5 (or_5_out, and_65_out, and_66_out);
  and and_125 (and_125_out, and_67_out, and_68_out);
  and and_126 (and_126_out, and_69_out, and_70_out);
  and and_127 (and_127_out, and_71_out, and_72_out);
  or or_6 (or_6_out, and_73_out, and_74_out);
  and and_128 (and_128_out, and_75_out, and_76_out);
  and and_129 (and_129_out, and_77_out, and_78_out);
  and and_130 (and_130_out, and_79_out, and_80_out);
  or or_7 (or_7_out, and_81_out, and_82_out);
  and and_131 (and_131_out, and_83_out, not_5_out);
  and and_132 (and_132_out, and_84_out, not_3_out);
  and and_133 (and_133_out, and_85_out, not_5_out);
  and and_134 (and_134_out, and_86_out, not_4_out);
  and and_135 (and_135_out, not_1_out, A0);
  and and_136 (and_136_out, and_87_out, A1);
  and and_137 (and_137_out, and_88_out, A1);
  or or_8 (or_8_out, and_89_out, and_90_out);
  and and_138 (and_138_out, and_91_out, not_5_out);
  and and_139 (and_139_out, and_92_out, not_3_out);
  and and_140 (and_140_out, and_93_out, not_5_out);
  and and_141 (and_141_out, and_94_out, not_4_out);
  and and_142 (and_142_out, not_1_out, A0);
  and and_143 (and_143_out, and_95_out, A1);
  and and_144 (and_144_out, and_96_out, A1);
  or or_9 (or_9_out, and_97_out, and_98_out);
  or or_10 (or_10_out, and_99_out, and_100_out);
  or or_11 (or_11_out, and_101_out, and_102_out);
  and and_145 (and_145_out, and_103_out, not_5_out);
  or or_12 (or_12_out, and_104_out, and_105_out);
  or or_13 (or_13_out, and_106_out, and_107_out);
  or or_14 (or_14_out, and_108_out, and_109_out);
  and and_146 (and_146_out, and_110_out, A0);
  or or_15 (or_15_out, and_111_out, and_112_out);
  or or_16 (or_16_out, and_113_out, and_114_out);
  or or_17 (or_17_out, and_115_out, and_116_out);
  and and_147 (and_147_out, and_117_out, not_5_out);
  or or_18 (or_18_out, and_118_out, and_119_out);
  or or_19 (or_19_out, and_120_out, and_121_out);
  or or_20 (or_20_out, and_122_out, and_123_out);
  and and_148 (and_148_out, and_124_out, A0);
  or or_21 (or_21_out, or_5_out, and_125_out);
  or or_22 (or_22_out, and_126_out, and_127_out);
  or or_23 (or_23_out, or_6_out, and_128_out);
  or or_24 (or_24_out, and_129_out, and_130_out);
  or or_25 (or_25_out, or_7_out, and_131_out);
  or or_26 (or_26_out, and_132_out, and_133_out);
  or or_27 (or_27_out, and_134_out, and_135_out);
  or or_28 (or_28_out, and_136_out, and_137_out);
  or or_29 (or_29_out, or_8_out, and_138_out);
  or or_30 (or_30_out, and_139_out, and_140_out);
  or or_31 (or_31_out, and_141_out, and_142_out);
  or or_32 (or_32_out, and_143_out, and_144_out);
  or or_33 (or_33_out, or_9_out, or_10_out);
  or or_34 (or_34_out, or_11_out, and_145_out);
  or or_35 (or_35_out, or_12_out, or_13_out);
  or or_36 (or_36_out, or_14_out, and_146_out);
  or or_37 (or_37_out, or_15_out, or_16_out);
  or or_38 (or_38_out, or_17_out, and_147_out);
  or or_39 (or_39_out, or_18_out, or_19_out);
  or or_40 (or_40_out, or_20_out, and_148_out);
  or or_41 (J2, or_21_out, or_22_out);
  or or_42 (K2, or_23_out, or_24_out);
  or or_43 (or_43_out, or_25_out, or_26_out);
  or or_44 (or_44_out, or_27_out, or_28_out);
  or or_45 (or_45_out, or_29_out, or_30_out);
  or or_46 (or_46_out, or_31_out, or_32_out);
  or or_47 (or_47_out, or_33_out, or_34_out);
  or or_48 (or_48_out, or_35_out, or_36_out);
  or or_49 (or_49_out, or_37_out, or_38_out);
  or or_50 (or_50_out, or_39_out, or_40_out);
  or or_51 (J1, or_43_out, or_44_out);
  or or_52 (K1, or_45_out, or_46_out);
  or or_53 (J0, or_47_out, or_48_out);
  or or_54 (K0, or_49_out, or_50_out);
endmodule

module COMBINACIONAL_2 (
  input  AUX,
  input  A3,
  input  A2,
  input  A1,
  input  A0,
  output JAUX,
  output KAUX,
  output J3,
  output K3,
  output J2,
  output K2,
  output J1,
  output K1,
  output J0,
  output K0
);

  wire and_1_out, and_2_out, and_3_out, and_4_out, and_5_out, and_6_out, and_7_out, and_8_out, and_9_out,
       and_10_out, and_11_out, and_12_out, and_13_out, and_14_out, and_15_out, and_16_out, and_17_out,
       and_18_out, and_19_out, and_20_out, and_21_out, and_22_out, and_23_out, and_24_out, and_25_out,
       and_26_out, and_27_out, and_28_out, and_29_out, and_30_out, and_31_out, and_32_out, and_33_out,
       and_34_out, and_35_out, and_36_out, and_37_out, and_38_out, and_39_out, and_40_out, and_41_out,
       and_42_out, and_43_out, and_44_out, and_45_out, and_46_out, and_47_out, and_48_out, and_49_out,
       and_50_out, and_51_out, and_52_out, and_53_out, and_54_out, and_55_out, and_56_out, and_57_out,
       and_58_out, and_59_out, and_60_out, and_61_out, and_62_out, and_63_out, and_64_out, and_65_out,
       and_66_out, and_67_out, and_68_out, and_69_out, and_70_out, and_71_out, and_72_out, and_73_out,
       and_74_out, and_75_out, and_76_out, and_77_out, and_78_out, and_79_out, and_80_out, and_81_out,
       and_82_out, and_83_out, and_84_out, and_85_out, and_86_out, and_87_out, and_88_out, and_89_out,
       and_90_out, and_91_out, and_92_out, and_93_out, and_94_out, and_95_out, and_96_out, and_97_out,
       and_98_out, and_99_out, and_100_out, and_101_out, and_102_out, and_103_out, and_104_out, and_105_out,
       and_106_out, and_107_out, and_108_out, and_109_out, and_110_out, and_111_out, and_112_out,
       and_113_out, and_114_out, and_115_out, and_116_out, and_117_out, and_118_out, and_119_out,
       and_120_out, and_121_out, and_122_out, and_123_out, and_124_out, and_125_out, and_126_out,
       and_127_out, and_128_out, and_129_out, and_130_out, and_131_out, and_132_out, and_133_out,
       and_134_out, and_135_out, and_136_out, and_137_out, and_138_out, and_139_out, and_140_out, not_1_out,
       not_2_out, not_3_out, not_4_out, not_5_out, or_1_out, or_2_out, or_3_out, or_4_out, or_5_out,
       or_6_out, or_7_out, or_8_out, or_9_out, or_10_out, or_11_out, or_12_out, or_13_out, or_14_out,
       or_15_out, or_16_out, or_17_out, or_18_out, or_19_out, or_20_out, or_21_out, or_22_out, or_23_out,
       or_24_out, or_25_out, or_26_out, or_27_out, or_28_out, or_29_out, or_30_out, or_31_out, or_32_out,
       or_33_out, or_34_out, or_35_out, or_36_out, or_37_out, or_38_out, or_43_out, or_44_out, or_45_out,
       or_46_out;

  not not_1 (not_1_out, AUX);
  not not_2 (not_2_out, A3);
  not not_3 (not_3_out, A2);
  not not_4 (not_4_out, A1);
  not not_5 (not_5_out, A0);
  and and_1 (and_1_out, AUX, not_2_out);
  and and_2 (and_2_out, AUX, not_2_out);
  and and_3 (and_3_out, not_1_out, not_2_out);
  and and_4 (and_4_out, A2, not_4_out);
  and and_5 (and_5_out, not_2_out, A2);
  and and_6 (and_6_out, not_1_out, not_2_out);
  and and_7 (and_7_out, A2, not_4_out);
  and and_8 (and_8_out, not_2_out, A2);
  and and_9 (and_9_out, not_1_out, not_2_out);
  and and_10 (and_10_out, not_1_out, A3);
  and and_11 (and_11_out, not_1_out, not_2_out);
  and and_12 (and_12_out, not_1_out, A3);
  and and_13 (and_13_out, not_1_out, A3);
  and and_14 (and_14_out, not_2_out, A2);
  and and_15 (and_15_out, not_4_out, not_5_out);
  and and_16 (and_16_out, not_2_out, not_3_out);
  and and_17 (and_17_out, not_4_out, A0);
  and and_18 (and_18_out, not_1_out, not_2_out);
  and and_19 (and_19_out, not_4_out, A0);
  and and_20 (and_20_out, not_1_out, A2);
  and and_21 (and_21_out, AUX, not_3_out);
  and and_22 (and_22_out, AUX, A1);
  and and_23 (and_23_out, AUX, A3);
  and and_24 (and_24_out, not_1_out, A3);
  and and_25 (and_25_out, not_2_out, A2);
  and and_26 (and_26_out, not_4_out, not_5_out);
  and and_27 (and_27_out, not_2_out, not_3_out);
  and and_28 (and_28_out, not_4_out, A0);
  and and_29 (and_29_out, not_1_out, not_2_out);
  and and_30 (and_30_out, not_4_out, A0);
  and and_31 (and_31_out, not_1_out, A2);
  and and_32 (and_32_out, AUX, not_3_out);
  and and_33 (and_33_out, AUX, A1);
  and and_34 (and_34_out, AUX, A3);
  and and_35 (and_35_out, not_3_out, A1);
  and and_36 (and_36_out, not_4_out, A0);
  and and_37 (and_37_out, not_1_out, A2);
  and and_38 (and_38_out, A3, A2);
  and and_39 (and_39_out, not_3_out, A1);
  and and_40 (and_40_out, not_4_out, A0);
  and and_41 (and_41_out, not_1_out, A2);
  and and_42 (and_42_out, A3, A2);
  and and_43 (and_43_out, and_1_out, A2);
  and and_44 (and_44_out, not_4_out, A0);
  and and_45 (and_45_out, not_1_out, A3);
  and and_46 (and_46_out, A2, A1);
  and and_47 (and_47_out, and_2_out, A2);
  and and_48 (and_48_out, not_4_out, A0);
  and and_49 (and_49_out, not_1_out, A3);
  and and_50 (and_50_out, A2, A1);
  and and_51 (and_51_out, and_3_out, and_4_out);
  and and_52 (and_52_out, and_5_out, A0);
  and and_53 (and_53_out, not_1_out, A3);
  and and_54 (and_54_out, not_3_out, not_4_out);
  and and_55 (and_55_out, not_1_out, A3);
  and and_56 (and_56_out, A2, A1);
  and and_57 (and_57_out, A2, A1);
  and and_58 (and_58_out, and_6_out, and_7_out);
  and and_59 (and_59_out, and_8_out, A0);
  and and_60 (and_60_out, not_1_out, A3);
  and and_61 (and_61_out, not_3_out, not_4_out);
  and and_62 (and_62_out, not_1_out, A3);
  and and_63 (and_63_out, A2, A1);
  and and_64 (and_64_out, A2, A1);
  and and_65 (and_65_out, and_9_out, not_3_out);
  and and_66 (and_66_out, not_4_out, not_5_out);
  and and_67 (and_67_out, not_2_out, A2);
  and and_68 (and_68_out, and_10_out, A2);
  and and_69 (and_69_out, A1, not_5_out);
  and and_70 (and_70_out, AUX, A1);
  and and_71 (and_71_out, and_11_out, not_3_out);
  and and_72 (and_72_out, not_4_out, not_5_out);
  and and_73 (and_73_out, not_2_out, A2);
  and and_74 (and_74_out, and_12_out, A2);
  and and_75 (and_75_out, A1, not_5_out);
  and and_76 (and_76_out, AUX, A1);
  and and_77 (and_77_out, and_13_out, A1);
  and and_78 (and_78_out, and_14_out, and_15_out);
  and and_79 (and_79_out, and_16_out, and_17_out);
  and and_80 (and_80_out, and_18_out, and_19_out);
  and and_81 (and_81_out, and_20_out, A0);
  and and_82 (and_82_out, and_21_out, A0);
  and and_83 (and_83_out, and_22_out, A0);
  and and_84 (and_84_out, and_23_out, A0);
  and and_85 (and_85_out, and_24_out, A1);
  and and_86 (and_86_out, and_25_out, and_26_out);
  and and_87 (and_87_out, and_27_out, and_28_out);
  and and_88 (and_88_out, and_29_out, and_30_out);
  and and_89 (and_89_out, and_31_out, A0);
  and and_90 (and_90_out, and_32_out, A0);
  and and_91 (and_91_out, and_33_out, A0);
  and and_92 (and_92_out, and_34_out, A0);
  or or_1 (or_1_out, and_35_out, and_36_out);
  and and_93 (and_93_out, not_1_out, not_2_out);
  and and_94 (and_94_out, and_37_out, not_4_out);
  and and_95 (and_95_out, not_2_out, not_3_out);
  and and_96 (and_96_out, not_2_out, A1);
  and and_97 (and_97_out, AUX, not_3_out);
  and and_98 (and_98_out, and_38_out, not_4_out);
  and and_99 (and_99_out, AUX, A1);
  or or_2 (or_2_out, and_39_out, and_40_out);
  and and_100 (and_100_out, not_1_out, not_2_out);
  and and_101 (and_101_out, and_41_out, not_4_out);
  and and_102 (and_102_out, not_2_out, not_3_out);
  and and_103 (and_103_out, not_2_out, A1);
  and and_104 (and_104_out, AUX, not_3_out);
  and and_105 (and_105_out, and_42_out, not_4_out);
  and and_106 (and_106_out, AUX, A1);
  and and_107 (and_107_out, and_43_out, and_44_out);
  and and_108 (and_108_out, and_45_out, and_46_out);
  and and_109 (and_109_out, A3, A2);
  and and_110 (and_110_out, A1, A0);
  and and_111 (and_111_out, and_47_out, and_48_out);
  and and_112 (and_112_out, and_49_out, and_50_out);
  and and_113 (and_113_out, A3, A2);
  and and_114 (and_114_out, A1, A0);
  or or_3 (or_3_out, and_51_out, and_52_out);
  and and_115 (and_115_out, and_53_out, and_54_out);
  and and_116 (and_116_out, and_55_out, and_56_out);
  and and_117 (and_117_out, and_57_out, A0);
  or or_4 (or_4_out, and_58_out, and_59_out);
  and and_118 (and_118_out, and_60_out, and_61_out);
  and and_119 (and_119_out, and_62_out, and_63_out);
  and and_120 (and_120_out, and_64_out, A0);
  and and_121 (and_121_out, and_65_out, and_66_out);
  and and_122 (and_122_out, and_67_out, A0);
  and and_123 (and_123_out, not_1_out, A3);
  and and_124 (and_124_out, not_3_out, A0);
  and and_125 (and_125_out, and_68_out, and_69_out);
  and and_126 (and_126_out, and_70_out, A0);
  and and_127 (and_127_out, not_2_out, A1);
  and and_128 (and_128_out, and_71_out, and_72_out);
  and and_129 (and_129_out, and_73_out, A0);
  and and_130 (and_130_out, not_1_out, A3);
  and and_131 (and_131_out, not_3_out, A0);
  and and_132 (and_132_out, and_74_out, and_75_out);
  and and_133 (and_133_out, and_76_out, A0);
  and and_134 (and_134_out, not_2_out, A1);
  or or_5 (or_5_out, and_77_out, and_78_out);
  or or_6 (or_6_out, and_79_out, and_80_out);
  or or_7 (or_7_out, and_81_out, and_82_out);
  or or_8 (or_8_out, and_83_out, and_84_out);
  or or_9 (or_9_out, and_85_out, and_86_out);
  or or_10 (or_10_out, and_87_out, and_88_out);
  or or_11 (or_11_out, and_89_out, and_90_out);
  or or_12 (or_12_out, and_91_out, and_92_out);
  or or_13 (or_13_out, or_1_out, and_93_out);
  or or_14 (or_14_out, and_94_out, and_95_out);
  or or_15 (or_15_out, and_96_out, and_97_out);
  or or_16 (or_16_out, and_98_out, and_99_out);
  or or_17 (or_17_out, or_2_out, and_100_out);
  or or_18 (or_18_out, and_101_out, and_102_out);
  or or_19 (or_19_out, and_103_out, and_104_out);
  or or_20 (or_20_out, and_105_out, and_106_out);
  or or_21 (or_21_out, and_107_out, and_108_out);
  and and_135 (and_135_out, and_109_out, and_110_out);
  or or_22 (or_22_out, and_111_out, and_112_out);
  and and_136 (and_136_out, and_113_out, and_114_out);
  or or_23 (or_23_out, or_3_out, and_115_out);
  or or_24 (or_24_out, and_116_out, and_117_out);
  or or_25 (or_25_out, or_4_out, and_118_out);
  or or_26 (or_26_out, and_119_out, and_120_out);
  or or_27 (or_27_out, and_121_out, and_122_out);
  and and_137 (and_137_out, and_123_out, and_124_out);
  or or_28 (or_28_out, and_125_out, and_126_out);
  and and_138 (and_138_out, and_127_out, A0);
  or or_29 (or_29_out, and_128_out, and_129_out);
  and and_139 (and_139_out, and_130_out, and_131_out);
  or or_30 (or_30_out, and_132_out, and_133_out);
  and and_140 (and_140_out, and_134_out, A0);
  or or_31 (or_31_out, or_5_out, or_6_out);
  or or_32 (or_32_out, or_7_out, or_8_out);
  or or_33 (or_33_out, or_9_out, or_10_out);
  or or_34 (or_34_out, or_11_out, or_12_out);
  or or_35 (or_35_out, or_13_out, or_14_out);
  or or_36 (or_36_out, or_15_out, or_16_out);
  or or_37 (or_37_out, or_17_out, or_18_out);
  or or_38 (or_38_out, or_19_out, or_20_out);
  or or_39 (JAUX, or_21_out, and_135_out);
  or or_40 (KAUX, or_22_out, and_136_out);
  or or_41 (J3, or_23_out, or_24_out);
  or or_42 (K3, or_25_out, or_26_out);
  or or_43 (or_43_out, or_27_out, and_137_out);
  or or_44 (or_44_out, or_28_out, and_138_out);
  or or_45 (or_45_out, or_29_out, and_139_out);
  or or_46 (or_46_out, or_30_out, and_140_out);
  or or_47 (J1, or_31_out, or_32_out);
  or or_48 (K1, or_33_out, or_34_out);
  or or_49 (J0, or_35_out, or_36_out);
  or or_50 (K0, or_37_out, or_38_out);
  or or_51 (J2, or_43_out, or_44_out);
  or or_52 (K2, or_45_out, or_46_out);
endmodule

module SOMADOR (
  input  A,
  input  B,
  input  Cin,
  output S,
  output Cout
);

  wire and_1_out, and_2_out, xor_1_out, xor_2_out;

  xor xor_1 (xor_1_out, A, B);
  xor xor_2 (xor_2_out, B, A);
  xor xor_3 (S, xor_1_out, Cin);
  and and_1 (and_1_out, A, B);
  and and_2 (and_2_out, Cin, xor_2_out);
  or or_1 (Cout, and_1_out, and_2_out);
endmodule

module SUBTRATOR (
  input  A,
  input  B,
  input  Cin,
  output S,
  output Cout
);

  wire and_1_out, and_2_out, and_3_out, not_1_out, or_1_out, xor_1_out;

  not not_1 (not_1_out, A);
  xor xor_1 (xor_1_out, A, B);
  and and_1 (and_1_out, not_1_out, Cin);
  and and_2 (and_2_out, not_1_out, B);
  xor xor_2 (S, xor_1_out, Cin);
  or or_1 (or_1_out, and_1_out, and_2_out);
  and and_3 (and_3_out, B, Cin);
  or or_2 (Cout, or_1_out, and_3_out);
endmodule

module SOMADOR_4 (
  input  A3,
  input  A2,
  input  A1,
  input  A0,
  input  ON_OFF,
  input  B3,
  input  B2,
  input  B1,
  input  B0,
  output S4,
  output S3,
  output S2,
  output S1,
  output S0
);

  wire and_1_out, and_2_out, and_3_out, and_4_out, and_5_out, and_6_out, and_7_out, and_8_out,
       somador_1_cout, somador_2_cout, somador_3_cout;

  and and_1 (and_1_out, A0, ON_OFF);
  and and_2 (and_2_out, A1, ON_OFF);
  and and_3 (and_3_out, A2, ON_OFF);
  and and_4 (and_4_out, A3, ON_OFF);
  and and_5 (and_5_out, ON_OFF, B0);
  and and_6 (and_6_out, ON_OFF, B1);
  and and_7 (and_7_out, ON_OFF, B2);
  and and_8 (and_8_out, ON_OFF, B3);
  SOMADOR somador_1 (.A(and_1_out), .B(and_5_out), .Cin(1'b0), .S(S0), .Cout(somador_1_cout));
  SOMADOR somador_2 (.A(and_2_out), .B(and_6_out), .Cin(somador_1_cout), .S(S1), .Cout(somador_2_cout));
  SOMADOR somador_3 (.A(and_3_out), .B(and_7_out), .Cin(somador_2_cout), .S(S2), .Cout(somador_3_cout));
  SOMADOR somador_4 (.A(and_4_out), .B(and_8_out), .Cin(somador_3_cout), .S(S3), .Cout(S4));
endmodule

module SUBTRATOR_4 (
  input  A3,
  input  A2,
  input  A1,
  input  A0,
  input  ON_OFF,
  input  B3,
  input  B2,
  input  B1,
  input  B0,
  output S4,
  output S3,
  output S2,
  output S1,
  output S0
);

  wire and_1_out, and_2_out, and_3_out, and_4_out, and_5_out, and_6_out, and_7_out, and_8_out,
       subtrator_1_cout, subtrator_2_cout, subtrator_3_cout;

  and and_1 (and_1_out, A0, ON_OFF);
  and and_2 (and_2_out, A1, ON_OFF);
  and and_3 (and_3_out, A2, ON_OFF);
  and and_4 (and_4_out, A3, ON_OFF);
  and and_5 (and_5_out, ON_OFF, B0);
  and and_6 (and_6_out, ON_OFF, B1);
  and and_7 (and_7_out, ON_OFF, B2);
  and and_8 (and_8_out, ON_OFF, B3);
  SUBTRATOR subtrator_1 (.A(and_1_out), .B(and_5_out), .Cin(1'b0), .S(S0), .Cout(subtrator_1_cout));
  SUBTRATOR subtrator_2 (.A(and_2_out), .B(and_6_out), .Cin(subtrator_1_cout), .S(S1), .Cout(subtrator_2_cout));
  SUBTRATOR subtrator_3 (.A(and_3_out), .B(and_7_out), .Cin(subtrator_2_cout), .S(S2), .Cout(subtrator_3_cout));
  SUBTRATOR subtrator_4 (.A(and_4_out), .B(and_8_out), .Cin(subtrator_3_cout), .S(S3), .Cout(S4));
endmodule

module AND_A_B (
  input  ON_OFF,
  input  A3,
  input  A2,
  input  A1,
  input  A0,
  input  B3,
  input  B2,
  input  B1,
  input  B0,
  output S3,
  output S2,
  output S1,
  output S0
);

  wire and_1_out, and_2_out, and_3_out, and_4_out, and_5_out, and_6_out, and_7_out, and_8_out;

  and and_1 (and_1_out, A3, ON_OFF);
  and and_2 (and_2_out, A2, ON_OFF);
  and and_3 (and_3_out, A1, ON_OFF);
  and and_4 (and_4_out, A0, ON_OFF);
  and and_5 (and_5_out, ON_OFF, B3);
  and and_6 (and_6_out, ON_OFF, B2);
  and and_7 (and_7_out, ON_OFF, B1);
  and and_8 (and_8_out, ON_OFF, B0);
  and and_9 (S3, and_1_out, and_5_out);
  and and_10 (S2, and_2_out, and_6_out);
  and and_11 (S1, and_3_out, and_7_out);
  and and_12 (S0, and_4_out, and_8_out);
endmodule

module OR_A_B (
  input  ON_OFF,
  input  A3,
  input  A2,
  input  A1,
  input  A0,
  input  B3,
  input  B2,
  input  B1,
  input  B0,
  output S3,
  output S2,
  output S1,
  output S0
);

  wire and_1_out, and_2_out, and_3_out, and_4_out, and_5_out, and_6_out, and_7_out, and_8_out;

  and and_1 (and_1_out, A3, ON_OFF);
  and and_2 (and_2_out, A2, ON_OFF);
  and and_3 (and_3_out, A1, ON_OFF);
  and and_4 (and_4_out, A0, ON_OFF);
  and and_5 (and_5_out, ON_OFF, B3);
  and and_6 (and_6_out, ON_OFF, B2);
  and and_7 (and_7_out, ON_OFF, B1);
  and and_8 (and_8_out, ON_OFF, B0);
  or or_1 (S3, and_1_out, and_5_out);
  or or_2 (S2, and_2_out, and_6_out);
  or or_3 (S1, and_3_out, and_7_out);
  or or_4 (S0, and_4_out, and_8_out);
endmodule

module SUBTRATOR_4_COMP2 (
  input  A3,
  input  A2,
  input  A1,
  input  A0,
  input  ON_OFF,
  input  B3,
  input  B2,
  input  B1,
  input  B0,
  output S3,
  output S2,
  output S1,
  output S0
);

  wire and_1_out, and_2_out, and_3_out, and_4_out, and_5_out, and_6_out, and_7_out, and_8_out,
       complemento_2_1_s0, complemento_2_1_s1, complemento_2_1_s2, complemento_2_1_s3;

  and and_1 (and_1_out, A0, ON_OFF);
  and and_2 (and_2_out, A2, ON_OFF);
  and and_3 (and_3_out, B3, ON_OFF);
  and and_4 (and_4_out, ON_OFF, B2);
  and and_5 (and_5_out, B1, ON_OFF);
  and and_6 (and_6_out, ON_OFF, B0);
  and and_7 (and_7_out, ON_OFF, A1);
  and and_8 (and_8_out, ON_OFF, A3);
  COMPLEMENTO_2 complemento_2_1 (
    .ON_OFF(ON_OFF), .A3(and_3_out), .A2(and_4_out), .A1(and_5_out), .A0(and_6_out), .S3(complemento_2_1_s3),
    .S2(complemento_2_1_s2), .S1(complemento_2_1_s1), .S0(complemento_2_1_s0));
  SOMADOR_4 somador_4_1 (
    .A3(and_8_out), .A2(and_2_out), .A1(and_7_out), .A0(and_1_out), .ON_OFF(ON_OFF), .B3(complemento_2_1_s3),
    .B2(complemento_2_1_s2), .B1(complemento_2_1_s1), .B0(complemento_2_1_s0), .S3(S3), .S2(S2), .S1(S1),
    .S0(S0));  // open: S4
endmodule

module NOT_A (
  input  ON_OFF,
  input  A3,
  input  A2,
  input  A1,
  input  A0,
  output S3,
  output S2,
  output S1,
  output S0
);

  wire not_1_out, not_2_out, not_3_out, not_4_out;

  not not_1 (not_1_out, A3);
  not not_2 (not_2_out, A2);
  not not_3 (not_3_out, A1);
  not not_4 (not_4_out, A0);
  and and_1 (S3, not_1_out, ON_OFF);
  and and_2 (S2, not_2_out, ON_OFF);
  and and_3 (S1, not_3_out, ON_OFF);
  and and_4 (S0, ON_OFF, not_4_out);
endmodule

module COMPLEMENTO_2 (
  input  ON_OFF,
  input  A3,
  input  A2,
  input  A1,
  input  A0,
  output S3,
  output S2,
  output S1,
  output S0
);

  wire not_a_1_s0, not_a_1_s1, not_a_1_s2, not_a_1_s3;

  NOT_A not_a_1 (
    .ON_OFF(ON_OFF), .A3(A3), .A2(A2), .A1(A1), .A0(A0), .S3(not_a_1_s3), .S2(not_a_1_s2), .S1(not_a_1_s1),
    .S0(not_a_1_s0));
  SOMADOR_4 somador_4_1 (
    .A3(not_a_1_s3), .A2(not_a_1_s2), .A1(not_a_1_s1), .A0(not_a_1_s0), .ON_OFF(ON_OFF), .B3(1'b0),
    .B2(1'b0), .B1(1'b0), .B0(1'b1), .S3(S3), .S2(S2), .S1(S1), .S0(S0));  // open: S4
endmodule

module COMPARADOR_A_B (
  input  ON_OFF,
  input  A3,
  input  A2,
  input  A1,
  input  A0,
  input  B3,
  input  B2,
  input  B1,
  input  B0,
  output S3,
  output S2,
  output S1,
  output S0
);

  wire and_1_out, and_2_out, and_3_out, and_4_out, and_5_out, and_6_out, and_7_out, and_8_out, not_1_out,
       not_2_out, not_3_out, not_4_out, xor_1_out, xor_2_out, xor_3_out, xor_4_out;

  and and_1 (and_1_out, A3, ON_OFF);
  and and_2 (and_2_out, A2, ON_OFF);
  and and_3 (and_3_out, A1, ON_OFF);
  and and_4 (and_4_out, A0, ON_OFF);
  and and_5 (and_5_out, ON_OFF, B3);
  and and_6 (and_6_out, ON_OFF, B2);
  and and_7 (and_7_out, ON_OFF, B1);
  and and_8 (and_8_out, ON_OFF, B0);
  xor xor_1 (xor_1_out, and_1_out, and_5_out);
  not not_1 (not_1_out, xor_1_out);
  xor xor_2 (xor_2_out, and_2_out, and_6_out);
  not not_2 (not_2_out, xor_2_out);
  xor xor_3 (xor_3_out, and_3_out, and_7_out);
  not not_3 (not_3_out, xor_3_out);
  xor xor_4 (xor_4_out, and_4_out, and_8_out);
  not not_4 (not_4_out, xor_4_out);
  and and_9 (S3, ON_OFF, not_1_out);
  and and_10 (S2, ON_OFF, not_2_out);
  and and_11 (S1, ON_OFF, not_3_out);
  and and_12 (S0, ON_OFF, not_4_out);
endmodule

module DISPLAY1 (
  input  a0,
  input  ON_OFF,
  output a,
  output b,
  output c,
  output d,
  output e,
  output f,
  output g
);

  wire not_1_out;

  not not_1 (not_1_out, a0);
  and and_1 (a, not_1_out, ON_OFF);
  and and_2 (d, not_1_out, ON_OFF);
  and and_3 (e, not_1_out, ON_OFF);
  and and_4 (f, not_1_out, ON_OFF);

  assign b = ON_OFF;
  assign c = ON_OFF;
  assign g = 1'b0;
endmodule

module DISPLAY_HEX (
  input  A3,
  input  A2,
  input  A1,
  input  A0,
  output a,
  output b,
  output c,
  output d,
  output e,
  output f,
  output g
);

  wire and_1_out, and_2_out, and_3_out, and_4_out, and_5_out, and_6_out, and_7_out, and_8_out, and_9_out,
       and_10_out, and_11_out, and_12_out, and_13_out, and_14_out, and_15_out, and_16_out, and_17_out,
       and_18_out, and_19_out, and_20_out, and_21_out, and_22_out, and_23_out, and_24_out, and_25_out,
       and_26_out, and_27_out, and_28_out, and_29_out, and_30_out, and_31_out, and_32_out, and_33_out,
       and_34_out, and_35_out, and_36_out, and_37_out, and_38_out, and_39_out, and_40_out, and_41_out,
       and_42_out, and_43_out, and_44_out, and_45_out, and_46_out, and_47_out, and_48_out, and_49_out,
       and_50_out, and_51_out, and_52_out, and_53_out, and_54_out, and_55_out, and_56_out, not_1_out,
       not_2_out, not_3_out, not_4_out, or_1_out, or_2_out, or_3_out, or_4_out, or_5_out, or_6_out, or_7_out,
       or_8_out, or_9_out, or_10_out, or_11_out, or_12_out, or_14_out, or_15_out, or_16_out, or_17_out,
       or_18_out, or_20_out, or_21_out, or_23_out, or_25_out, or_27_out, or_28_out, or_30_out, or_31_out,
       or_33_out;

  not not_1 (not_1_out, A3);
  not not_2 (not_2_out, A2);
  not not_3 (not_3_out, A1);
  not not_4 (not_4_out, A0);
  and and_1 (and_1_out, A3, not_2_out);
  and and_2 (and_2_out, not_1_out, not_3_out);
  and and_3 (and_3_out, not_1_out, A1);
  and and_4 (and_4_out, not_1_out, A2);
  and and_5 (and_5_out, A3, not_2_out);
  and and_6 (and_6_out, A2, not_3_out);
  and and_7 (and_7_out, not_1_out, not_2_out);
  and and_8 (and_8_out, not_1_out, not_2_out);
  and and_9 (and_9_out, not_1_out, A1);
  and and_10 (and_10_out, not_2_out, not_3_out);
  and and_11 (and_11_out, A3, not_2_out);
  and and_12 (and_12_out, A2, A1);
  and and_13 (and_13_out, not_2_out, not_4_out);
  and and_14 (and_14_out, A1, not_4_out);
  and and_15 (and_15_out, A3, A1);
  and and_16 (and_16_out, A3, A2);
  and and_17 (and_17_out, not_1_out, A2);
  and and_18 (and_18_out, not_1_out, A2);
  and and_19 (and_19_out, not_1_out, A2);
  and and_20 (and_20_out, A2, not_3_out);
  and and_21 (and_21_out, not_2_out, not_4_out);
  and and_22 (and_22_out, not_1_out, A1);
  and and_23 (and_23_out, not_1_out, A2);
  and and_24 (and_24_out, and_1_out, not_3_out);
  and and_25 (and_25_out, A3, not_4_out);
  and and_26 (and_26_out, and_2_out, not_4_out);
  and and_27 (and_27_out, and_3_out, A0);
  and and_28 (and_28_out, A3, not_3_out);
  or or_1 (or_1_out, and_4_out, and_5_out);
  and and_29 (and_29_out, not_3_out, A0);
  and and_30 (and_30_out, not_1_out, not_3_out);
  and and_31 (and_31_out, not_1_out, A0);
  and and_32 (and_32_out, and_6_out, A0);
  and and_33 (and_33_out, and_7_out, not_4_out);
  and and_34 (and_34_out, and_8_out, A1);
  and and_35 (and_35_out, and_9_out, not_4_out);
  and and_36 (and_36_out, and_10_out, not_4_out);
  and and_37 (and_37_out, and_11_out, A0);
  and and_38 (and_38_out, A3, not_3_out);
  and and_39 (and_39_out, and_12_out, not_4_out);
  or or_2 (or_2_out, and_13_out, and_14_out);
  or or_3 (or_3_out, and_15_out, and_16_out);
  and and_40 (and_40_out, not_3_out, not_4_out);
  and and_41 (and_41_out, and_17_out, not_3_out);
  and and_42 (and_42_out, not_2_out, A1);
  and and_43 (and_43_out, A3, not_2_out);
  and and_44 (and_44_out, and_18_out, not_3_out);
  and and_45 (and_45_out, and_19_out, not_4_out);
  and and_46 (and_46_out, and_20_out, A0);
  and and_47 (and_47_out, A1, not_4_out);
  or or_4 (or_4_out, and_21_out, and_22_out);
  and and_48 (and_48_out, and_23_out, A0);
  or or_5 (or_5_out, and_24_out, and_25_out);
  and and_49 (and_49_out, A2, A1);
  or or_6 (or_6_out, and_26_out, and_27_out);
  and and_50 (and_50_out, not_2_out, not_4_out);
  and and_51 (and_51_out, and_28_out, A0);
  and and_52 (and_52_out, not_1_out, not_2_out);
  or or_7 (or_7_out, or_1_out, and_29_out);
  or or_8 (or_8_out, and_30_out, and_31_out);
  or or_9 (or_9_out, and_32_out, and_33_out);
  or or_10 (or_10_out, and_34_out, and_35_out);
  or or_11 (or_11_out, and_36_out, and_37_out);
  or or_12 (or_12_out, and_38_out, and_39_out);
  or or_13 (e, or_2_out, or_3_out);
  or or_14 (or_14_out, and_40_out, and_41_out);
  and and_53 (and_53_out, A2, not_4_out);
  and and_54 (and_54_out, A3, not_2_out);
  and and_55 (and_55_out, A3, A1);
  or or_15 (or_15_out, and_42_out, and_43_out);
  or or_16 (or_16_out, and_44_out, and_45_out);
  or or_17 (or_17_out, and_46_out, and_47_out);
  and and_56 (and_56_out, A3, A0);
  or or_18 (or_18_out, or_4_out, and_48_out);
  or or_19 (a, or_18_out, or_20_out);
  or or_20 (or_20_out, or_5_out, and_49_out);
  or or_21 (or_21_out, or_6_out, and_50_out);
  or or_22 (b, or_21_out, or_23_out);
  or or_23 (or_23_out, and_51_out, and_52_out);
  or or_24 (c, or_7_out, or_8_out);
  or or_25 (or_25_out, or_9_out, or_10_out);
  or or_26 (d, or_25_out, or_27_out);
  or or_27 (or_27_out, or_11_out, or_12_out);
  or or_28 (or_28_out, or_14_out, and_53_out);
  or or_29 (f, or_28_out, or_30_out);
  or or_30 (or_30_out, and_54_out, and_55_out);
  or or_31 (or_31_out, or_15_out, or_16_out);
  or or_32 (g, or_31_out, or_33_out);
  or or_33 (or_33_out, or_17_out, and_56_out);
endmodule

module DISPLAY4 (
  input  a3,
  input  a2,
  input  a1,
  input  a0,
  input  ON_OFF,
  output a,
  output b,
  output c,
  output d,
  output e,
  output f,
  output g
);

  wire and_1_out, and_2_out, and_3_out, and_4_out, and_5_out, and_6_out, and_7_out, and_8_out, and_9_out,
       and_10_out, and_11_out, and_12_out, and_13_out, and_14_out, and_15_out, and_16_out, and_17_out,
       and_18_out, and_19_out, and_20_out, and_21_out, and_22_out, and_23_out, and_24_out, and_25_out,
       and_26_out, and_27_out, and_28_out, and_29_out, and_30_out, and_31_out, and_32_out, and_33_out,
       and_34_out, and_35_out, and_36_out, and_37_out, and_38_out, and_39_out, and_40_out, and_41_out,
       and_42_out, and_43_out, and_44_out, and_45_out, and_46_out, and_47_out, and_48_out, and_49_out,
       and_50_out, and_51_out, and_52_out, and_53_out, and_54_out, and_55_out, and_56_out, and_57_out,
       and_58_out, and_59_out, and_60_out, and_61_out, and_62_out, and_63_out, and_64_out, and_65_out,
       and_66_out, and_67_out, and_68_out, and_69_out, and_70_out, and_71_out, and_72_out, and_73_out,
       and_74_out, and_75_out, and_76_out, and_77_out, and_78_out, and_79_out, and_80_out, and_81_out,
       and_82_out, and_83_out, and_84_out, and_85_out, and_86_out, and_87_out, and_88_out, and_89_out,
       and_90_out, and_91_out, and_92_out, and_93_out, and_94_out, and_95_out, and_96_out, not_1_out,
       not_2_out, not_3_out, not_4_out, or_1_out, or_2_out, or_3_out, or_4_out, or_5_out, or_6_out, or_7_out,
       or_8_out, or_9_out, or_10_out, or_11_out, or_12_out, or_13_out, or_14_out, or_15_out, or_16_out,
       or_17_out, or_18_out, or_19_out, or_20_out, or_21_out, or_22_out, or_24_out, or_25_out, or_26_out,
       or_27_out;

  not not_1 (not_1_out, a3);
  not not_2 (not_2_out, a2);
  not not_3 (not_3_out, a1);
  not not_4 (not_4_out, a0);
  and and_1 (and_1_out, not_2_out, not_4_out);
  and and_2 (and_2_out, a3, not_2_out);
  and and_3 (and_3_out, not_3_out, ON_OFF);
  and and_4 (and_4_out, a3, not_4_out);
  and and_5 (and_5_out, not_1_out, a2);
  and and_6 (and_6_out, a0, ON_OFF);
  and and_7 (and_7_out, not_2_out, not_4_out);
  and and_8 (and_8_out, not_1_out, not_3_out);
  and and_9 (and_9_out, not_4_out, ON_OFF);
  and and_10 (and_10_out, a3, not_2_out);
  and and_11 (and_11_out, not_3_out, a0);
  and and_12 (and_12_out, a2, not_3_out);
  and and_13 (and_13_out, a0, ON_OFF);
  and and_14 (and_14_out, not_2_out, not_3_out);
  and and_15 (and_15_out, not_4_out, ON_OFF);
  and and_16 (and_16_out, a3, not_2_out);
  and and_17 (and_17_out, a0, ON_OFF);
  and and_18 (and_18_out, not_1_out, not_2_out);
  and and_19 (and_19_out, not_4_out, ON_OFF);
  and and_20 (and_20_out, not_1_out, not_2_out);
  and and_21 (and_21_out, a1, ON_OFF);
  and and_22 (and_22_out, a3, not_3_out);
  and and_23 (and_23_out, not_1_out, a1);
  and and_24 (and_24_out, not_4_out, ON_OFF);
  and and_25 (and_25_out, a3, a2);
  and and_26 (and_26_out, not_4_out, ON_OFF);
  and and_27 (and_27_out, not_2_out, not_4_out);
  and and_28 (and_28_out, a3, a1);
  and and_29 (and_29_out, a3, a2);
  and and_30 (and_30_out, a1, not_4_out);
  and and_31 (and_31_out, not_3_out, not_4_out);
  and and_32 (and_32_out, a3, not_2_out);
  and and_33 (and_33_out, a3, not_2_out);
  and and_34 (and_34_out, not_2_out, a1);
  and and_35 (and_35_out, not_1_out, a2);
  and and_36 (and_36_out, not_3_out, ON_OFF);
  and and_37 (and_37_out, a2, not_3_out);
  and and_38 (and_38_out, a0, ON_OFF);
  and and_39 (and_39_out, not_1_out, a2);
  and and_40 (and_40_out, not_4_out, ON_OFF);
  and and_41 (and_41_out, a1, not_4_out);
  and and_42 (and_42_out, and_1_out, ON_OFF);
  or or_1 (or_1_out, and_42_out, and_43_out);
  and and_43 (and_43_out, and_2_out, and_3_out);
  and and_44 (and_44_out, not_1_out, a1);
  and and_45 (and_45_out, and_44_out, ON_OFF);
  and and_46 (and_46_out, and_4_out, ON_OFF);
  or or_2 (or_2_out, and_46_out, and_47_out);
  and and_47 (and_47_out, and_5_out, and_6_out);
  and and_48 (and_48_out, a2, a1);
  and and_49 (and_49_out, and_48_out, ON_OFF);
  and and_50 (and_50_out, and_7_out, ON_OFF);
  or or_3 (or_3_out, and_50_out, and_51_out);
  and and_51 (and_51_out, and_8_out, and_9_out);
  and and_52 (and_52_out, a3, not_3_out);
  and and_53 (and_53_out, and_52_out, and_54_out);
  and and_54 (and_54_out, a0, ON_OFF);
  and and_55 (and_55_out, not_1_out, a1);
  and and_56 (and_56_out, and_55_out, and_57_out);
  and and_57 (and_57_out, a0, ON_OFF);
  and and_58 (and_58_out, not_2_out, not_3_out);
  and and_59 (and_59_out, and_58_out, ON_OFF);
  and and_60 (and_60_out, and_10_out, ON_OFF);
  or or_4 (or_4_out, and_60_out, and_61_out);
  and and_61 (and_61_out, and_11_out, ON_OFF);
  and and_62 (and_62_out, not_1_out, a2);
  and and_63 (and_63_out, and_62_out, ON_OFF);
  and and_64 (and_64_out, not_2_out, not_3_out);
  and and_65 (and_65_out, and_64_out, ON_OFF);
  and and_66 (and_66_out, not_2_out, a0);
  and and_67 (and_67_out, and_66_out, ON_OFF);
  and and_68 (and_68_out, and_12_out, and_13_out);
  or or_5 (or_5_out, and_68_out, and_69_out);
  and and_69 (and_69_out, and_14_out, and_15_out);
  and and_70 (and_70_out, and_16_out, and_17_out);
  or or_6 (or_6_out, and_70_out, and_71_out);
  and and_71 (and_71_out, and_18_out, and_19_out);
  and and_72 (and_72_out, and_20_out, and_21_out);
  or or_7 (or_7_out, and_72_out, and_73_out);
  and and_73 (and_73_out, and_22_out, ON_OFF);
  and and_74 (and_74_out, and_23_out, and_24_out);
  or or_8 (or_8_out, and_74_out, and_75_out);
  and and_75 (and_75_out, and_25_out, and_26_out);
  and and_76 (and_76_out, and_27_out, ON_OFF);
  or or_9 (or_9_out, and_76_out, and_77_out);
  and and_77 (and_77_out, and_28_out, ON_OFF);
  and and_78 (and_78_out, and_29_out, ON_OFF);
  or or_10 (or_10_out, and_78_out, and_79_out);
  and and_79 (and_79_out, and_30_out, ON_OFF);
  and and_80 (and_80_out, and_31_out, ON_OFF);
  or or_11 (or_11_out, and_80_out, and_81_out);
  and and_81 (and_81_out, and_32_out, ON_OFF);
  and and_82 (and_82_out, not_1_out, a2);
  and and_83 (and_83_out, and_82_out, and_84_out);
  and and_84 (and_84_out, not_3_out, ON_OFF);
  and and_85 (and_85_out, a2, not_4_out);
  and and_86 (and_86_out, and_85_out, ON_OFF);
  and and_87 (and_87_out, a3, a1);
  and and_88 (and_88_out, and_87_out, ON_OFF);
  and and_89 (and_89_out, and_33_out, ON_OFF);
  or or_12 (or_12_out, and_89_out, and_90_out);
  and and_90 (and_90_out, and_34_out, ON_OFF);
  and and_91 (and_91_out, and_35_out, and_36_out);
  or or_13 (or_13_out, and_91_out, and_92_out);
  and and_92 (and_92_out, and_37_out, and_38_out);
  and and_93 (and_93_out, and_39_out, and_40_out);
  or or_14 (or_14_out, and_93_out, and_94_out);
  and and_94 (and_94_out, and_41_out, ON_OFF);
  and and_95 (and_95_out, a3, a0);
  and and_96 (and_96_out, and_95_out, ON_OFF);
  or or_15 (or_15_out, or_1_out, and_45_out);
  or or_16 (or_16_out, or_2_out, and_49_out);
  or or_17 (or_17_out, or_3_out, and_53_out);
  or or_18 (or_18_out, and_56_out, and_59_out);
  or or_19 (or_19_out, or_4_out, and_63_out);
  or or_20 (or_20_out, and_65_out, and_67_out);
  or or_21 (or_21_out, or_5_out, or_6_out);
  or or_22 (or_22_out, or_7_out, or_8_out);
  or or_23 (e, or_9_out, or_10_out);
  or or_24 (or_24_out, or_11_out, and_83_out);
  or or_25 (or_25_out, and_86_out, and_88_out);
  or or_26 (or_26_out, or_12_out, or_13_out);
  or or_27 (or_27_out, or_14_out, and_96_out);
  or or_28 (a, or_15_out, or_16_out);
  or or_29 (b, or_17_out, or_18_out);
  or or_30 (c, or_19_out, or_20_out);
  or or_31 (d, or_21_out, or_22_out);
  or or_32 (f, or_24_out, or_25_out);
  or or_33 (g, or_26_out, or_27_out);
endmodule

module DISPLAY5_DECIMAL (
  input  ON_OFF,
  input  a4,
  input  a3,
  input  a2,
  input  a1,
  input  a0,
  output a,
  output b,
  output c,
  output d,
  output e,
  output f,
  output g
);

  wire and_1_out, and_2_out, and_3_out, and_4_out, and_5_out, and_6_out, and_7_out, and_8_out, and_9_out,
       and_10_out, and_11_out, and_12_out, and_13_out, and_14_out, and_15_out, and_16_out, and_17_out,
       and_18_out, and_19_out, and_20_out, and_21_out, and_22_out, and_23_out, and_24_out, and_25_out,
       and_26_out, and_27_out, and_28_out, and_29_out, and_30_out, and_31_out, and_32_out, and_33_out,
       and_34_out, and_35_out, and_36_out, and_37_out, and_38_out, and_39_out, and_40_out, and_41_out,
       and_42_out, and_43_out, and_44_out, and_45_out, and_46_out, and_47_out, and_48_out, and_49_out,
       and_50_out, and_51_out, and_52_out, and_53_out, and_54_out, and_55_out, and_56_out, and_57_out,
       and_58_out, and_59_out, and_60_out, and_61_out, and_62_out, and_63_out, and_64_out, and_65_out,
       and_66_out, and_67_out, and_68_out, and_69_out, and_70_out, and_71_out, and_72_out, and_73_out,
       and_74_out, and_75_out, and_76_out, and_77_out, and_78_out, and_79_out, and_80_out, and_81_out,
       and_82_out, and_83_out, and_84_out, and_85_out, and_86_out, and_87_out, and_88_out, and_89_out,
       and_90_out, and_91_out, and_92_out, and_93_out, and_94_out, and_95_out, and_96_out, and_97_out,
       and_98_out, and_99_out, and_100_out, and_101_out, and_102_out, and_103_out, and_104_out, and_105_out,
       and_106_out, and_107_out, and_108_out, and_109_out, and_110_out, and_111_out, and_112_out,
       and_113_out, and_114_out, and_115_out, and_116_out, and_117_out, and_118_out, and_119_out,
       and_120_out, and_121_out, and_122_out, and_123_out, and_124_out, and_125_out, and_126_out,
       and_127_out, and_128_out, and_129_out, and_130_out, and_131_out, and_132_out, and_133_out,
       and_134_out, and_135_out, and_136_out, and_137_out, and_138_out, and_139_out, and_140_out,
       and_141_out, and_142_out, and_143_out, and_144_out, and_145_out, and_146_out, and_147_out,
       and_148_out, and_149_out, and_150_out, and_151_out, and_152_out, and_153_out, and_154_out,
       and_155_out, and_156_out, and_157_out, and_158_out, and_159_out, and_160_out, and_161_out,
       and_162_out, and_163_out, and_164_out, and_165_out, and_166_out, and_167_out, and_168_out,
       and_169_out, and_170_out, and_171_out, and_172_out, and_173_out, and_174_out, and_175_out,
       and_176_out, and_177_out, and_178_out, and_179_out, and_180_out, and_181_out, and_182_out,
       and_183_out, and_184_out, and_185_out, and_186_out, and_187_out, and_188_out, and_189_out,
       and_190_out, and_191_out, and_192_out, and_193_out, and_194_out, and_195_out, and_196_out,
       and_197_out, and_198_out, and_199_out, and_200_out, and_201_out, and_202_out, and_203_out,
       and_204_out, and_205_out, and_206_out, and_207_out, and_208_out, and_209_out, and_210_out, not_1_out,
       not_2_out, not_3_out, not_4_out, not_5_out, or_1_out, or_2_out, or_3_out, or_4_out, or_5_out,
       or_6_out, or_7_out, or_8_out, or_9_out, or_10_out, or_11_out, or_12_out, or_13_out, or_14_out,
       or_15_out, or_16_out, or_17_out, or_18_out, or_19_out, or_20_out, or_21_out, or_22_out, or_23_out,
       or_24_out, or_25_out, or_26_out, or_27_out, or_28_out, or_29_out, or_30_out, or_31_out, or_32_out,
       or_33_out, or_34_out, or_35_out, or_36_out, or_37_out, or_38_out, or_39_out, or_40_out, or_41_out,
       or_42_out, or_43_out, or_44_out, or_45_out, or_46_out, or_47_out, or_48_out, or_49_out, or_50_out,
       or_51_out, or_52_out, or_53_out, or_54_out, or_56_out, or_60_out, or_61_out;

  not not_1 (not_1_out, a4);
  not not_2 (not_2_out, a3);
  not not_3 (not_3_out, a2);
  not not_4 (not_4_out, a1);
  not not_5 (not_5_out, a0);
  and and_1 (and_1_out, ON_OFF, not_2_out);
  and and_2 (and_2_out, ON_OFF, not_1_out);
  and and_3 (and_3_out, a2, a0);
  and and_4 (and_4_out, ON_OFF, not_1_out);
  and and_5 (and_5_out, a3, not_4_out);
  and and_6 (and_6_out, ON_OFF, not_2_out);
  and and_7 (and_7_out, not_3_out, not_5_out);
  and and_8 (and_8_out, ON_OFF, a4);
  and and_9 (and_9_out, not_2_out, not_5_out);
  and and_10 (and_10_out, ON_OFF, a4);
  and and_11 (and_11_out, not_3_out, a0);
  and and_12 (and_12_out, ON_OFF, not_2_out);
  and and_13 (and_13_out, a1, a0);
  and and_14 (and_14_out, ON_OFF, a3);
  and and_15 (and_15_out, not_4_out, not_5_out);
  and and_16 (and_16_out, ON_OFF, not_1_out);
  and and_17 (and_17_out, ON_OFF, not_1_out);
  and and_18 (and_18_out, not_4_out, not_5_out);
  and and_19 (and_19_out, ON_OFF, not_1_out);
  and and_20 (and_20_out, a3, not_4_out);
  and and_21 (and_21_out, ON_OFF, not_1_out);
  and and_22 (and_22_out, a3, not_5_out);
  and and_23 (and_23_out, ON_OFF, not_2_out);
  and and_24 (and_24_out, not_3_out, a0);
  and and_25 (and_25_out, ON_OFF, not_2_out);
  and and_26 (and_26_out, not_3_out, a1);
  and and_27 (and_27_out, ON_OFF, a2);
  and and_28 (and_28_out, not_4_out, not_5_out);
  and and_29 (and_29_out, ON_OFF, a4);
  and and_30 (and_30_out, not_2_out, a0);
  and and_31 (and_31_out, ON_OFF, a4);
  and and_32 (and_32_out, not_2_out, a1);
  and and_33 (and_33_out, ON_OFF, not_3_out);
  and and_34 (and_34_out, a1, a0);
  and and_35 (and_35_out, ON_OFF, a3);
  and and_36 (and_36_out, a2, not_4_out);
  and and_37 (and_37_out, ON_OFF, a3);
  and and_38 (and_38_out, a2, not_5_out);
  and and_39 (and_39_out, ON_OFF, a4);
  and and_40 (and_40_out, ON_OFF, not_1_out);
  and and_41 (and_41_out, ON_OFF, not_1_out);
  and and_42 (and_42_out, ON_OFF, not_1_out);
  and and_43 (and_43_out, ON_OFF, a3);
  and and_44 (and_44_out, ON_OFF, not_1_out);
  and and_45 (and_45_out, ON_OFF, not_1_out);
  and and_46 (and_46_out, ON_OFF, a4);
  and and_47 (and_47_out, ON_OFF, not_1_out);
  and and_48 (and_48_out, ON_OFF, not_2_out);
  and and_49 (and_49_out, not_3_out, a1);
  and and_50 (and_50_out, ON_OFF, not_1_out);
  and and_51 (and_51_out, a2, not_4_out);
  and and_52 (and_52_out, ON_OFF, a3);
  and and_53 (and_53_out, ON_OFF, not_1_out);
  and and_54 (and_54_out, a3, a2);
  and and_55 (and_55_out, ON_OFF, a4);
  and and_56 (and_56_out, not_3_out, not_5_out);
  and and_57 (and_57_out, ON_OFF, a4);
  and and_58 (and_58_out, not_2_out, a1);
  and and_59 (and_59_out, and_1_out, a1);
  and and_60 (and_60_out, and_2_out, and_3_out);
  and and_61 (and_61_out, ON_OFF, not_1_out);
  and and_62 (and_62_out, not_3_out, not_5_out);
  and and_63 (and_63_out, and_4_out, and_5_out);
  and and_64 (and_64_out, and_6_out, and_7_out);
  and and_65 (and_65_out, ON_OFF, a4);
  and and_66 (and_66_out, not_2_out, not_3_out);
  and and_67 (and_67_out, and_8_out, and_9_out);
  and and_68 (and_68_out, and_10_out, and_11_out);
  and and_69 (and_69_out, ON_OFF, not_3_out);
  and and_70 (and_70_out, a1, not_5_out);
  and and_71 (and_71_out, ON_OFF, a3);
  and and_72 (and_72_out, a2, not_4_out);
  and and_73 (and_73_out, ON_OFF, a4);
  and and_74 (and_74_out, a1, not_5_out);
  and and_75 (and_75_out, and_12_out, and_13_out);
  and and_76 (and_76_out, and_14_out, and_15_out);
  and and_77 (and_77_out, and_16_out, not_3_out);
  and and_78 (and_78_out, and_17_out, and_18_out);
  and and_79 (and_79_out, and_19_out, and_20_out);
  and and_80 (and_80_out, and_21_out, and_22_out);
  and and_81 (and_81_out, and_23_out, and_24_out);
  and and_82 (and_82_out, and_25_out, and_26_out);
  and and_83 (and_83_out, and_27_out, and_28_out);
  and and_84 (and_84_out, and_29_out, and_30_out);
  and and_85 (and_85_out, and_31_out, and_32_out);
  and and_86 (and_86_out, and_33_out, and_34_out);
  and and_87 (and_87_out, and_35_out, and_36_out);
  and and_88 (and_88_out, and_37_out, and_38_out);
  and and_89 (and_89_out, ON_OFF, a4);
  and and_90 (and_90_out, a1, a0);
  and and_91 (and_91_out, ON_OFF, a0);
  and and_92 (and_92_out, and_39_out, not_3_out);
  and and_93 (and_93_out, ON_OFF, not_2_out);
  and and_94 (and_94_out, ON_OFF, not_1_out);
  and and_95 (and_95_out, not_2_out, a2);
  and and_96 (and_96_out, ON_OFF, not_3_out);
  and and_97 (and_97_out, ON_OFF, a3);
  and and_98 (and_98_out, ON_OFF, not_1_out);
  and and_99 (and_99_out, a2, a1);
  and and_100 (and_100_out, ON_OFF, a4);
  and and_101 (and_101_out, ON_OFF, a3);
  and and_102 (and_102_out, ON_OFF, not_2_out);
  and and_103 (and_103_out, not_3_out, a1);
  and and_104 (and_104_out, and_40_out, a2);
  and and_105 (and_105_out, not_4_out, a0);
  and and_106 (and_106_out, ON_OFF, not_2_out);
  and and_107 (and_107_out, a1, not_5_out);
  and and_108 (and_108_out, and_41_out, a3);
  and and_109 (and_109_out, a2, a0);
  and and_110 (and_110_out, ON_OFF, a4);
  and and_111 (and_111_out, not_2_out, a1);
  and and_112 (and_112_out, ON_OFF, a3);
  and and_113 (and_113_out, not_4_out, a0);
  and and_114 (and_114_out, ON_OFF, not_1_out);
  and and_115 (and_115_out, a3, not_4_out);
  and and_116 (and_116_out, ON_OFF, not_2_out);
  and and_117 (and_117_out, not_3_out, not_5_out);
  and and_118 (and_118_out, ON_OFF, not_3_out);
  and and_119 (and_119_out, a1, not_5_out);
  and and_120 (and_120_out, ON_OFF, a3);
  and and_121 (and_121_out, a2, not_4_out);
  and and_122 (and_122_out, ON_OFF, not_2_out);
  and and_123 (and_123_out, a1, not_5_out);
  and and_124 (and_124_out, ON_OFF, not_2_out);
  and and_125 (and_125_out, not_3_out, not_5_out);
  and and_126 (and_126_out, ON_OFF, not_1_out);
  and and_127 (and_127_out, not_3_out, not_5_out);
  and and_128 (and_128_out, and_42_out, a3);
  and and_129 (and_129_out, not_4_out, not_5_out);
  and and_130 (and_130_out, ON_OFF, a4);
  and and_131 (and_131_out, not_2_out, not_5_out);
  and and_132 (and_132_out, ON_OFF, not_3_out);
  and and_133 (and_133_out, a1, not_5_out);
  and and_134 (and_134_out, and_43_out, a2);
  and and_135 (and_135_out, not_4_out, not_5_out);
  and and_136 (and_136_out, ON_OFF, a4);
  and and_137 (and_137_out, a1, not_5_out);
  and and_138 (and_138_out, and_44_out, not_2_out);
  and and_139 (and_139_out, a2, not_4_out);
  and and_140 (and_140_out, ON_OFF, a3);
  and and_141 (and_141_out, not_3_out, not_4_out);
  and and_142 (and_142_out, and_45_out, a3);
  and and_143 (and_143_out, a2, a1);
  and and_144 (and_144_out, and_46_out, not_2_out);
  and and_145 (and_145_out, not_3_out, a1);
  and and_146 (and_146_out, ON_OFF, a4);
  and and_147 (and_147_out, a3, not_4_out);
  and and_148 (and_148_out, ON_OFF, not_2_out);
  and and_149 (and_149_out, not_4_out, not_5_out);
  and and_150 (and_150_out, ON_OFF, a3);
  and and_151 (and_151_out, a1, not_5_out);
  and and_152 (and_152_out, and_47_out, not_2_out);
  and and_153 (and_153_out, a2, not_5_out);
  and and_154 (and_154_out, and_48_out, and_49_out);
  and and_155 (and_155_out, and_50_out, and_51_out);
  and and_156 (and_156_out, and_52_out, not_4_out);
  and and_157 (and_157_out, and_53_out, and_54_out);
  and and_158 (and_158_out, and_55_out, and_56_out);
  and and_159 (and_159_out, and_57_out, and_58_out);
  and and_160 (and_160_out, ON_OFF, not_2_out);
  and and_161 (and_161_out, a1, not_5_out);
  or or_1 (or_1_out, and_59_out, and_60_out);
  and and_162 (and_162_out, and_61_out, and_62_out);
  or or_2 (or_2_out, and_63_out, and_64_out);
  and and_163 (and_163_out, and_65_out, and_66_out);
  or or_3 (or_3_out, and_67_out, and_68_out);
  and and_164 (and_164_out, and_69_out, and_70_out);
  and and_165 (and_165_out, and_71_out, and_72_out);
  and and_166 (and_166_out, and_73_out, and_74_out);
  or or_4 (or_4_out, and_75_out, and_76_out);
  or or_5 (or_5_out, and_77_out, and_78_out);
  or or_6 (or_6_out, and_79_out, and_80_out);
  or or_7 (or_7_out, and_81_out, and_82_out);
  or or_8 (or_8_out, and_83_out, and_84_out);
  or or_9 (or_9_out, and_85_out, and_86_out);
  or or_10 (or_10_out, and_87_out, and_88_out);
  and and_167 (and_167_out, and_89_out, and_90_out);
  or or_11 (or_11_out, and_91_out, and_92_out);
  and and_168 (and_168_out, and_93_out, not_4_out);
  and and_169 (and_169_out, and_94_out, and_95_out);
  and and_170 (and_170_out, and_96_out, not_4_out);
  and and_171 (and_171_out, and_97_out, not_3_out);
  and and_172 (and_172_out, and_98_out, and_99_out);
  and and_173 (and_173_out, and_100_out, not_4_out);
  and and_174 (and_174_out, and_101_out, a1);
  and and_175 (and_175_out, and_102_out, and_103_out);
  and and_176 (and_176_out, and_104_out, and_105_out);
  and and_177 (and_177_out, and_106_out, and_107_out);
  and and_178 (and_178_out, and_108_out, and_109_out);
  and and_179 (and_179_out, and_110_out, and_111_out);
  and and_180 (and_180_out, and_112_out, and_113_out);
  and and_181 (and_181_out, ON_OFF, not_1_out);
  and and_182 (and_182_out, not_3_out, not_5_out);
  and and_183 (and_183_out, and_114_out, and_115_out);
  and and_184 (and_184_out, and_116_out, and_117_out);
  and and_185 (and_185_out, ON_OFF, a4);
  and and_186 (and_186_out, not_2_out, not_5_out);
  and and_187 (and_187_out, and_118_out, and_119_out);
  and and_188 (and_188_out, and_120_out, and_121_out);
  and and_189 (and_189_out, ON_OFF, a4);
  and and_190 (and_190_out, a1, not_5_out);
  and and_191 (and_191_out, and_122_out, and_123_out);
  and and_192 (and_192_out, and_124_out, and_125_out);
  and and_193 (and_193_out, and_126_out, and_127_out);
  and and_194 (and_194_out, and_128_out, and_129_out);
  and and_195 (and_195_out, and_130_out, and_131_out);
  and and_196 (and_196_out, and_132_out, and_133_out);
  and and_197 (and_197_out, and_134_out, and_135_out);
  and and_198 (and_198_out, and_136_out, and_137_out);
  and and_199 (and_199_out, and_138_out, and_139_out);
  and and_200 (and_200_out, and_140_out, and_141_out);
  and and_201 (and_201_out, and_142_out, and_143_out);
  and and_202 (and_202_out, and_144_out, and_145_out);
  and and_203 (and_203_out, and_146_out, and_147_out);
  and and_204 (and_204_out, and_148_out, and_149_out);
  and and_205 (and_205_out, and_150_out, and_151_out);
  and and_206 (and_206_out, and_152_out, and_153_out);
  or or_12 (or_12_out, and_154_out, and_155_out);
  or or_13 (or_13_out, and_156_out, and_157_out);
  or or_14 (or_14_out, and_158_out, and_159_out);
  and and_207 (and_207_out, and_160_out, and_161_out);
  or or_15 (or_15_out, or_1_out, and_162_out);
  or or_16 (or_16_out, or_15_out, or_17_out);
  or or_17 (or_17_out, or_2_out, and_163_out);
  or or_18 (or_18_out, or_3_out, and_164_out);
  or or_19 (or_19_out, or_18_out, or_20_out);
  or or_20 (or_20_out, and_165_out, and_166_out);
  or or_21 (or_21_out, or_4_out, or_5_out);
  or or_22 (or_22_out, or_21_out, or_23_out);
  or or_23 (or_23_out, or_6_out, or_7_out);
  or or_24 (or_24_out, or_8_out, or_9_out);
  or or_25 (or_25_out, or_24_out, or_26_out);
  or or_26 (or_26_out, or_10_out, and_167_out);
  or or_27 (or_27_out, or_11_out, and_168_out);
  or or_28 (or_28_out, or_27_out, or_29_out);
  or or_29 (or_29_out, and_169_out, and_170_out);
  or or_30 (or_30_out, and_171_out, and_172_out);
  or or_31 (or_31_out, or_30_out, or_32_out);
  or or_32 (or_32_out, and_173_out, and_174_out);
  or or_33 (or_33_out, and_175_out, and_176_out);
  or or_34 (or_34_out, or_33_out, or_35_out);
  or or_35 (or_35_out, and_177_out, and_178_out);
  or or_36 (or_36_out, and_179_out, and_180_out);
  or or_37 (or_37_out, or_36_out, and_208_out);
  and and_208 (and_208_out, and_181_out, and_182_out);
  or or_38 (or_38_out, and_183_out, and_184_out);
  or or_39 (or_39_out, or_38_out, and_209_out);
  and and_209 (and_209_out, and_185_out, and_186_out);
  or or_40 (or_40_out, and_187_out, and_188_out);
  or or_41 (or_41_out, or_40_out, and_210_out);
  and and_210 (and_210_out, and_189_out, and_190_out);
  or or_42 (or_42_out, and_191_out, and_192_out);
  or or_43 (or_43_out, or_42_out, or_44_out);
  or or_44 (or_44_out, and_193_out, and_194_out);
  or or_45 (or_45_out, and_195_out, and_196_out);
  or or_46 (or_46_out, or_45_out, or_47_out);
  or or_47 (or_47_out, and_197_out, and_198_out);
  or or_48 (or_48_out, and_199_out, and_200_out);
  or or_49 (or_49_out, or_48_out, or_50_out);
  or or_50 (or_50_out, and_201_out, and_202_out);
  or or_51 (or_51_out, and_203_out, and_204_out);
  or or_52 (or_52_out, or_51_out, or_53_out);
  or or_53 (or_53_out, and_205_out, and_206_out);
  or or_54 (or_54_out, or_12_out, or_13_out);
  or or_55 (g, or_54_out, or_56_out);
  or or_56 (or_56_out, or_14_out, and_207_out);
  or or_57 (a, or_16_out, or_19_out);
  or or_58 (b, or_22_out, or_25_out);
  or or_59 (c, or_28_out, or_31_out);
  or or_60 (or_60_out, or_34_out, or_37_out);
  or or_61 (or_61_out, or_39_out, or_41_out);
  or or_62 (e, or_43_out, or_46_out);
  or or_63 (f, or_49_out, or_52_out);
  or or_64 (d, or_60_out, or_61_out);
endmodule
module DISPLAY5_DECIMAL_BIT_MAIS_SIGN (
  input  ON_OFF,
  input  a4,
  input  a3,
  input  a2,
  input  a1,
  input  a0,
  output a,
  output b,
  output c,
  output d,
  output e,
  output f,
  output g
);

  wire and_1_out, and_2_out, and_3_out, and_4_out, and_5_out, and_6_out, and_7_out, and_8_out, and_9_out,
       and_10_out, and_11_out, and_12_out, and_13_out, and_14_out, and_15_out, and_16_out, and_17_out,
       and_18_out, and_19_out, and_20_out, and_21_out, and_22_out, and_23_out, and_24_out, and_25_out,
       and_26_out, and_27_out, and_28_out, and_29_out, and_30_out, and_31_out, and_32_out, and_33_out,
       and_34_out, and_35_out, and_36_out, and_37_out, and_38_out, and_39_out, and_40_out, and_41_out,
       and_42_out, and_43_out, and_44_out, and_45_out, and_46_out, not_1_out, not_2_out, not_3_out,
       not_4_out, or_1_out, or_2_out, or_3_out, or_4_out, or_5_out, or_6_out, or_12_out, or_14_out;

  not not_1 (not_1_out, a4);
  not not_2 (not_2_out, a3);
  not not_3 (not_3_out, a2);
  not not_4 (not_4_out, a1);
  and and_1 (and_1_out, ON_OFF, not_1_out);
  and and_2 (and_2_out, ON_OFF, a4);
  and and_3 (and_3_out, ON_OFF, not_1_out);
  and and_4 (and_4_out, not_3_out, not_4_out);
  and and_5 (and_5_out, ON_OFF, not_2_out);
  and and_6 (and_6_out, ON_OFF, not_2_out);
  and and_7 (and_7_out, ON_OFF, not_1_out);
  and and_8 (and_8_out, ON_OFF, a4);
  and and_9 (and_9_out, ON_OFF, not_1_out);
  and and_10 (and_10_out, not_3_out, not_4_out);
  and and_11 (and_11_out, ON_OFF, not_2_out);
  and and_12 (and_12_out, ON_OFF, not_1_out);
  and and_13 (and_13_out, ON_OFF, not_2_out);
  and and_14 (and_14_out, ON_OFF, not_1_out);
  and and_15 (and_15_out, ON_OFF, not_1_out);
  and and_16 (and_16_out, not_3_out, not_4_out);
  and and_17 (and_17_out, ON_OFF, a4);
  and and_18 (and_18_out, ON_OFF, a4);
  and and_19 (and_19_out, and_1_out, not_2_out);
  and and_20 (and_20_out, and_2_out, a3);
  and and_21 (and_21_out, and_3_out, and_4_out);
  and and_22 (and_22_out, and_5_out, a2);
  and and_23 (and_23_out, ON_OFF, not_1_out);
  and and_24 (and_24_out, and_6_out, not_3_out);
  and and_25 (and_25_out, ON_OFF, a3);
  and and_26 (and_26_out, a2, a1);
  and and_27 (and_27_out, and_7_out, not_2_out);
  and and_28 (and_28_out, and_8_out, a3);
  and and_29 (and_29_out, and_9_out, and_10_out);
  and and_30 (and_30_out, and_11_out, a2);
  and and_31 (and_31_out, and_12_out, not_2_out);
  and and_32 (and_32_out, and_13_out, a2);
  and and_33 (and_33_out, ON_OFF, a4);
  and and_34 (and_34_out, a3, not_3_out);
  and and_35 (and_35_out, ON_OFF, not_1_out);
  and and_36 (and_36_out, not_3_out, not_4_out);
  and and_37 (and_37_out, ON_OFF, a4);
  and and_38 (and_38_out, a2, not_4_out);
  and and_39 (and_39_out, and_14_out, not_2_out);
  and and_40 (and_40_out, and_15_out, and_16_out);
  and and_41 (and_41_out, and_17_out, a2);
  and and_42 (and_42_out, and_18_out, a3);
  or or_1 (or_1_out, and_19_out, and_20_out);
  or or_2 (or_2_out, and_21_out, and_22_out);
  or or_3 (or_3_out, and_23_out, and_24_out);
  and and_43 (and_43_out, and_25_out, and_26_out);
  or or_4 (or_4_out, and_27_out, and_28_out);
  or or_5 (or_5_out, and_29_out, and_30_out);
  or or_6 (or_6_out, and_31_out, and_32_out);
  and and_44 (and_44_out, and_33_out, and_34_out);
  and and_45 (and_45_out, and_35_out, and_36_out);
  and and_46 (and_46_out, and_37_out, and_38_out);
  or or_7 (f, and_39_out, and_40_out);
  or or_8 (g, and_41_out, and_42_out);
  or or_9 (a, or_1_out, or_2_out);
  or or_10 (c, or_3_out, and_43_out);
  or or_11 (d, or_4_out, or_5_out);
  or or_12 (or_12_out, or_6_out, and_44_out);
  or or_13 (e, or_12_out, or_14_out);
  or or_14 (or_14_out, and_45_out, and_46_out);

  assign b = ON_OFF;
endmodule

module MUX_8_1 (
  input  E0,
  input  E1,
  input  E2,
  input  E3,
  input  E4,
  input  E5,
  input  E6,
  input  E7,
  input  S2,
  input  S1,
  input  S0,
  output O
);

  wire mux_4_1_1_o, mux_4_1_2_o;

  MUX_4_1 mux_4_1_1 (.E0(E0), .E1(E1), .E2(E2), .E3(E3), .S1(S1), .S0(S0), .O(mux_4_1_1_o));
  MUX_4_1 mux_4_1_2 (.E0(E4), .E1(E5), .E2(E6), .E3(E7), .S1(S1), .S0(S0), .O(mux_4_1_2_o));
  MUX_2_1 mux_2_1_1 (.E0(mux_4_1_1_o), .E1(mux_4_1_2_o), .SEL(S2), .S(O));
endmodule

module MUX_4_1 (
  input  E0,
  input  E1,
  input  E2,
  input  E3,
  input  S1,
  input  S0,
  output O
);

  wire mux_2_1_1_s, mux_2_1_2_s;

  MUX_2_1 mux_2_1_1 (.E0(E0), .E1(E1), .SEL(S0), .S(mux_2_1_1_s));
  MUX_2_1 mux_2_1_2 (.E0(E2), .E1(E3), .SEL(S0), .S(mux_2_1_2_s));
  MUX_2_1 mux_2_1_3 (.E0(mux_2_1_1_s), .E1(mux_2_1_2_s), .SEL(S1), .S(O));
endmodule

module MUX_2_1 (
  input  E0,
  input  E1,
  input  SEL,
  output S
);

  wire and_1_out, and_2_out;

  and and_1 (and_1_out, E0, ~SEL);  // AND_Gate
  and and_2 (and_2_out, E1, SEL);
  or or_1 (S, and_1_out, and_2_out);
endmodule

module FF_JK_MS_SR (
  input  PRESET,
  input  J,
  input  CLK,
  input  K,
  input  CLEAR,
  output Q,
  output nQ
);

  wire and_1_out, and_2_out, display_hex_1_a, display_hex_1_b, display_hex_1_c, display_hex_1_d,
       display_hex_1_e, display_hex_1_f, display_hex_1_g;

  and and_1 (and_1_out, J, nQ);
  and and_2 (and_2_out, Q, K);
  S_R_Flip_Flop s_r_ff_1 (.S(and_1_out), .R(and_2_out), .clk(CLK), .Q(Q), .reset(CLEAR), .Qn(nQ), .preset(PRESET));
  _7_Segment_Display u_7_segment_display_1 (
    .g(display_hex_1_g), .f(display_hex_1_f), .a(display_hex_1_a), .b(display_hex_1_b), .e(display_hex_1_e),
    .d(display_hex_1_d), .c(display_hex_1_c));  // open: dp
  DISPLAY_HEX display_hex_1 (
    .A1(1'b0), .A0(Q), .A3(1'b0), .A2(1'b0), .c(display_hex_1_c), .d(display_hex_1_d), .e(display_hex_1_e),
    .f(display_hex_1_f), .g(display_hex_1_g), .a(display_hex_1_a), .b(display_hex_1_b));
endmodule

module CLEAR_PRESET (
  input  E,
  input  ENABLE,
  output PRESET,
  output CLEAR
);

  wire not_1_out;

  not not_1 (not_1_out, E);
  and and_1 (PRESET, E, ENABLE);
  and and_2 (CLEAR, not_1_out, ENABLE);
endmodule

module DEMUX_1_8 (
  input  E,
  input  S2,
  input  S1,
  input  S0,
  output O0,
  output O1,
  output O2,
  output O3,
  output O4,
  output O5,
  output O6,
  output O7
);

  wire demux_1_2_1_o0, demux_1_2_1_o1;

  DEMUX_1_2 demux_1_2_1 (.E(E), .S(S2), .O0(demux_1_2_1_o0), .O1(demux_1_2_1_o1));
  DEMUX_1_4 demux_1_4_1 (.E(demux_1_2_1_o0), .S1(S1), .S0(S0), .O0(O0), .O1(O1), .O2(O2), .O3(O3));
  DEMUX_1_4 demux_1_4_2 (.E(demux_1_2_1_o1), .S1(S1), .S0(S0), .O0(O4), .O1(O5), .O2(O6), .O3(O7));
endmodule

module DEMUX_1_4 (
  input  E,
  input  S1,
  input  S0,
  output O0,
  output O1,
  output O2,
  output O3
);

  wire demux_1_2_1_o0, demux_1_2_1_o1;

  DEMUX_1_2 demux_1_2_1 (.E(E), .S(S1), .O0(demux_1_2_1_o0), .O1(demux_1_2_1_o1));
  DEMUX_1_2 demux_1_2_2 (.E(demux_1_2_1_o0), .S(S0), .O0(O0), .O1(O1));
  DEMUX_1_2 demux_1_2_3 (.E(demux_1_2_1_o1), .S(S0), .O0(O2), .O1(O3));
endmodule

module DEMUX_1_2 (
  input  E,
  input  S,
  output O0,
  output O1
);

  and and_1 (O0, ~S, E);  // AND_Gate
  and and_2 (O1, S, E);
endmodule
